// Logisim project ALU_shreyam.circ as structural Verilog: 4 circuits, main circuit 1-bit ALU
module _1_bit_ALU (
  input  [2:0] SC,
  input  [19:0] IR,
  input  DR_i,
  input  in_4,
  input  in_5,
  input  in_6,
  input  INPR__i,
  input  AC_i_1,
  input  AC_i_1_2,
  output out_10,
  output out_11
);

  wire adder_1_out, adder_2_out, adder_3_out, and_1_out, and_2_out, and_3_out, and_4_out, and_5_out,
       and_6_out, and_7_out, and_8_out, and_9_out, and_10_out, and_11_out, button_1_out,
       demultiplexer_1_out0, demultiplexer_1_out1, demultiplexer_1_out2, demultiplexer_1_out3,
       demultiplexer_1_out4, demultiplexer_1_out5, demultiplexer_1_out6, demultiplexer_1_out7,
       demultiplexer_1_out8, not_1_out, not_2_out, not_3_out, or_1_out, or_2_out;
  wire [3:0] alu_control_1_out_3;

  Demultiplexer #(.select(4), .enable("false")) demultiplexer_1 (
    .out0(demultiplexer_1_out0), .out1(demultiplexer_1_out1), .out2(demultiplexer_1_out2),
    .out3(demultiplexer_1_out3), .out4(demultiplexer_1_out4), .out5(demultiplexer_1_out5),
    .out6(demultiplexer_1_out6), .out7(demultiplexer_1_out7), .out8(demultiplexer_1_out8), .in(1'b1),
    .sel(alu_control_1_out_3));  // open: out9, out10, out11, out12, out13, out14, out15
  ALU_Control alu_control_1 (.SC(SC), .in_1(IR), .out_3(alu_control_1_out_3));
  not not_1 (not_1_out, DR_i);
  Adder #(.width(1)) adder_1 (.a(1'b1), .b(not_1_out), .out(adder_1_out));  // open: cin, cout
  not not_2 (not_2_out, out_10);
  or or_1 (or_1_out, out_10, DR_i);
  Adder #(.width(1)) adder_2 (.a(out_10), .b(DR_i), .out(adder_2_out), .cin(in_5), .cout(out_11));
  Adder #(.width(1)) adder_3 (.a(out_10), .b(adder_1_out), .out(adder_3_out));  // open: cin, cout
  and and_1 (and_1_out, demultiplexer_1_out0, out_10, DR_i);
  and and_2 (and_2_out, demultiplexer_1_out1, or_1_out);
  and and_3 (and_3_out, demultiplexer_1_out2, adder_2_out);
  and and_4 (and_4_out, demultiplexer_1_out3, adder_3_out);
  and and_5 (and_5_out, demultiplexer_1_out4, DR_i);
  and and_6 (and_6_out, demultiplexer_1_out5, INPR__i);
  and and_7 (and_7_out, demultiplexer_1_out6, not_2_out);
  and and_8 (and_8_out, demultiplexer_1_out7, AC_i_1);
  and and_9 (and_9_out, demultiplexer_1_out8, AC_i_1_2);
  or or_2 (or_2_out, and_1_out, and_2_out, and_3_out, and_4_out, and_5_out, and_6_out, and_7_out, and_8_out, and_9_out);
  not not_3 (not_3_out, or_2_out);
  and and_10 (and_10_out, in_6, or_2_out);
  and and_11 (and_11_out, not_3_out, in_6);
  J_K_Flip_Flop j_k_ff_1 (
    .J(and_10_out), .clk(in_4), .K(and_11_out), .Q(out_10), .reset(button_1_out));  // open: Qn, preset, en
  Button button_1 (.out(button_1_out));

  // Notes on the sheet:
  //   AND
  //   OR
  //   ADD
  //   SUB
  //   DR
  //   INPR
  //   COM
  //   SHR
  //   SHL
endmodule

module ALU_1_bit__with_pins (
  input  DR_i,
  input  AND,
  input  OR,
  input  ADD,
  input  in_5,
  input  in_6,
  input  in_7,
  input  SUB,
  input  DR__signal,
  input  INPR__signal,
  input  INPR__i,
  input  COM,
  input  SHR,
  input  AC_i_1,
  input  SHL,
  input  AC_i_1_2,
  output out_17,
  output out_18
);

  wire adder_1_out, adder_2_out, adder_3_out, and_1_out, and_2_out, and_3_out, and_4_out, and_5_out,
       and_6_out, and_7_out, and_8_out, and_9_out, and_10_out, and_11_out, button_1_out, not_1_out,
       not_2_out, not_3_out, or_1_out, or_2_out;

  not not_1 (not_1_out, DR_i);
  not not_2 (not_2_out, out_17);
  Adder #(.width(1)) adder_1 (.a(1'b1), .b(not_1_out), .out(adder_1_out));  // open: cin, cout
  or or_1 (or_1_out, out_17, DR_i);
  Adder #(.width(1)) adder_2 (.a(out_17), .b(DR_i), .out(adder_2_out), .cin(in_6), .cout(out_18));
  Adder #(.width(1)) adder_3 (.a(out_17), .b(adder_1_out), .out(adder_3_out));  // open: cin, cout
  and and_1 (and_1_out, AND, out_17, DR_i);
  and and_2 (and_2_out, OR, or_1_out);
  and and_3 (and_3_out, ADD, adder_2_out);
  and and_4 (and_4_out, SUB, adder_3_out);
  and and_5 (and_5_out, DR__signal, DR_i);
  and and_6 (and_6_out, INPR__signal, INPR__i);
  and and_7 (and_7_out, COM, not_2_out);
  and and_8 (and_8_out, SHR, AC_i_1);
  and and_9 (and_9_out, SHL, AC_i_1_2);
  or or_2 (or_2_out, and_1_out, and_2_out, and_3_out, and_4_out, and_5_out, and_6_out, and_7_out, and_8_out, and_9_out);
  not not_3 (not_3_out, or_2_out);
  and and_10 (and_10_out, in_7, or_2_out);
  and and_11 (and_11_out, not_3_out, in_7);
  J_K_Flip_Flop j_k_ff_1 (
    .J(and_10_out), .clk(in_5), .K(and_11_out), .Q(out_17), .reset(button_1_out));  // open: Qn, preset, en
  Button button_1 (.out(button_1_out));
endmodule

module ALU_Control (
  input  [19:0] in_1,
  input  [2:0] SC,
  output [3:0] out_3
);

  wire ADD_out, AND_4_out, and_5_out, and_6_out, COM, decoder_1_out0, decoder_1_out1, decoder_1_out2,
       decoder_1_out3, decoder_1_out4, decoder_1_out5, decoder_1_out6, decoder_1_out7, decoder_2_out0,
       decoder_2_out1, decoder_2_out2, decoder_2_out3, decoder_2_out4, decoder_2_out5, decoder_2_out6,
       decoder_2_out7, decoder_2_out8, decoder_2_out9, decoder_2_out10, decoder_2_out11, decoder_2_out12,
       decoder_2_out13, decoder_2_out14, decoder_2_out15, DR_out, INPR, not_1_out, or_2_out, OR_out, p, r,
       SHL, SHR, SUB_out;

  Decoder #(.select(3), .enable("false")) decoder_1 (
    .out0(decoder_1_out0), .out1(decoder_1_out1), .out2(decoder_1_out2), .out3(decoder_1_out3),
    .out4(decoder_1_out4), .out5(decoder_1_out5), .out6(decoder_1_out6), .out7(decoder_1_out7), .sel(SC));
  Decoder #(.select(4), .enable("false")) decoder_2 (
    .out0(decoder_2_out0), .out1(decoder_2_out1), .out2(decoder_2_out2), .out3(decoder_2_out3),
    .out4(decoder_2_out4), .out5(decoder_2_out5), .out6(decoder_2_out6), .out7(decoder_2_out7),
    .out8(decoder_2_out8), .out9(decoder_2_out9), .out10(decoder_2_out10), .out11(decoder_2_out11),
    .out12(decoder_2_out12), .out13(decoder_2_out13), .out14(decoder_2_out14), .out15(decoder_2_out15),
    .sel(in_1[17:14]));
  and and_1 (r, decoder_2_out0, in_1[18], in_1[19], decoder_1_out3);
  and and_2 (p, decoder_2_out15, in_1[18], in_1[19], decoder_1_out3);
  and and_3 (INPR, p, in_1[13]);
  and AND_4 (AND_4_out, decoder_1_out5, decoder_2_out0);
  and OR (OR_out, decoder_1_out5, decoder_2_out1);
  and ADD (ADD_out, decoder_1_out5, decoder_2_out2);
  and SUB (SUB_out, decoder_1_out5, decoder_2_out3);
  and and_5 (and_5_out, decoder_1_out5, decoder_2_out4);
  and and_6 (and_6_out, decoder_1_out6, decoder_2_out9);
  and and_7 (SHL, in_1[8], r);
  or DR (DR_out, and_5_out, and_6_out);
  and and_8 (SHR, in_1[9], r);
  and and_9 (COM, in_1[11], r);
  not not_1 (not_1_out, or_2_out);
  or or_2 (or_2_out, COM, SHR, AND_4_out, OR_out, SUB_out, DR_out, SHL, COM, ADD_out);
  Priority_Encoder #(.select(4)) priority_encoder_1 (
    .in0(not_1_out), .in1(AND_4_out), .in2(OR_out), .in3(ADD_out), .in4(SUB_out), .in5(DR_out), .in6(INPR),
    .in7(COM), .in8(SHR), .in9(SHL), .in10(1'b0), .in11(1'b0), .in12(1'b0), .in13(1'b0), .in14(1'b0),
    .in15(1'b0), .out(out_3));  // open: gs, en_out, en_in
endmodule

module _20_bit_ALU (
  input  [2:0] SC,
  input  [19:0] IR,
  input  [19:0] DR,
  input  in_4,
  input  in_5,
  input  [19:0] INPR,
  output [19:0] out_7,
  output out_8
);

  wire button_1_out, or_3_out;
  wire [3:0] alu_control_1_out_3;
  wire [19:0] adder_1_out, adder_2_out, adder_3_out, and_1_out, and_2_out, and_3_out, and_4_out, and_5_out,
       and_6_out, and_7_out, and_8_out, and_9_out, demultiplexer_1_out1, demultiplexer_1_out2,
       demultiplexer_1_out3, demultiplexer_1_out4, demultiplexer_1_out5, demultiplexer_1_out6,
       demultiplexer_1_out7, demultiplexer_1_out8, demultiplexer_1_out9, not_1_out, not_2_out, or_1_out,
       or_2_out, shifter_1_out, shifter_2_out;

  Demultiplexer #(.select(4), .width(20), .enable("false")) demultiplexer_1 (
    .out1(demultiplexer_1_out1), .out2(demultiplexer_1_out2), .out3(demultiplexer_1_out3),
    .out4(demultiplexer_1_out4), .out5(demultiplexer_1_out5), .out6(demultiplexer_1_out6),
    .out7(demultiplexer_1_out7), .out8(demultiplexer_1_out8), .out9(demultiplexer_1_out9), .in({20{1'b1}}),
    .sel(alu_control_1_out_3));  // open: out0, out10, out11, out12, out13, out14, out15
  ALU_Control alu_control_1 (.SC(SC), .in_1(IR), .out_3(alu_control_1_out_3));
  Shifter #(.width(20), .shift("rr")) shifter_1 (.in(out_7), .\dist (5'b00001), .out(shifter_1_out));
  Shifter #(.width(20), .shift("rl")) shifter_2 (.in(out_7), .\dist (5'b00001), .out(shifter_2_out));
  assign not_1_out = ~DR;  // NOT_Gate not_1, 20 bits wide
  Adder #(.width(20)) adder_1 (.a({20{1'b1}}), .b(not_1_out), .out(adder_1_out));  // open: cin, cout
  assign not_2_out = ~out_7;  // NOT_Gate not_2, 20 bits wide
  assign or_1_out = out_7 | DR;  // OR_Gate or_1, 20 bits wide
  Adder #(.width(20)) adder_2 (.a(out_7), .b(DR), .out(adder_2_out), .cin(in_4), .cout(out_8));
  Adder #(.width(20)) adder_3 (.a(out_7), .b(adder_1_out), .out(adder_3_out));  // open: cin, cout
  assign and_1_out = demultiplexer_1_out1 & out_7 & DR;  // AND_Gate and_1, 20 bits wide
  assign and_2_out = demultiplexer_1_out2 & or_1_out;  // AND_Gate and_2, 20 bits wide
  assign and_3_out = demultiplexer_1_out3 & adder_2_out;  // AND_Gate and_3, 20 bits wide
  assign and_4_out = demultiplexer_1_out4 & adder_3_out;  // AND_Gate and_4, 20 bits wide
  assign and_5_out = demultiplexer_1_out5 & DR;  // AND_Gate and_5, 20 bits wide
  assign and_6_out = demultiplexer_1_out6 & INPR;  // AND_Gate and_6, 20 bits wide
  assign and_7_out = demultiplexer_1_out7 & not_2_out;  // AND_Gate and_7, 20 bits wide
  assign and_8_out = demultiplexer_1_out8 & shifter_1_out;  // AND_Gate and_8, 20 bits wide
  assign and_9_out = demultiplexer_1_out9 & shifter_2_out;  // AND_Gate and_9, 20 bits wide
  assign or_2_out = and_1_out | and_2_out | and_3_out | and_4_out | and_5_out | and_6_out | and_7_out | and_8_out | and_9_out;  // OR_Gate or_2, 20 bits wide
  or or_3 (or_3_out, alu_control_1_out_3[3], alu_control_1_out_3[2], alu_control_1_out_3[1], alu_control_1_out_3[0]);
  Button button_1 (.out(button_1_out));
  Register #(.width(20)) register_1 (.D(or_2_out), .en(or_3_out), .Q(out_7), .clk(in_5), .clr(button_1_out));

  // Notes on the sheet:
  //   AND
  //   OR
  //   ADD
  //   SUB
  //   DR
  //   INPR
  //   COM
  //   SHR
  //   SHL
endmodule
