// Logisim project Final draft design.circ as structural Verilog: 39 circuits, main circuit Final
module PC (
  input  [19:0] Common_Bus,
  input  Clear,
  input  Load,
  input  Increment,
  input  Clk,
  output [19:0] OUT
);

  wire or_1_out;
  wire [13:0] adder_1_out, multiplexer_1_out;

  Multiplexer #(.width(14), .enable("false")) multiplexer_1 (
    .in0(Common_Bus[13:0]), .in1(adder_1_out), .out(multiplexer_1_out), .sel(Increment));
  Adder #(.width(14)) adder_1 (.a(14'h1), .b(OUT[13:0]), .out(adder_1_out));  // open: cin, cout
  or or_1 (or_1_out, Increment, Load);
  Register #(.width(14), .trigger("falling")) register_1 (
    .D(multiplexer_1_out), .en(or_1_out), .Q(OUT[13:0]), .clk(Clk), .clr(Clear));

  assign OUT[19:14] = {6{1'b0}};
endmodule

// PC Control
module PC_control (
  input  [19:0] IR,
  input  [2:0] SC,
  input  [19:0] AC,
  input  [19:0] DR,
  input  R,
  input  FGI,
  input  FGO,
  input  E,
  output Load,
  output Increment,
  output Clear
);

  wire and_3_out, and_4_out, and_5_out, and_6_out, and_7_out, and_8_out, and_9_out, and_10_out, and_11_out,
       and_12_out, and_13_out, decoder_1_out0, decoder_1_out1, decoder_1_out2, decoder_1_out3,
       decoder_1_out4, decoder_1_out5, decoder_1_out6, decoder_1_out7, decoder_2_out0, decoder_2_out1,
       decoder_2_out2, decoder_2_out3, decoder_2_out4, decoder_2_out5, decoder_2_out6, decoder_2_out7,
       decoder_2_out8, decoder_2_out9, decoder_2_out10, decoder_2_out11, decoder_2_out12, decoder_2_out13,
       decoder_2_out14, decoder_2_out15, or_1_out, or_2_out, p, r_t;

  Decoder #(.select(3)) decoder_1 (
    .out0(decoder_1_out0), .out1(decoder_1_out1), .out2(decoder_1_out2), .out3(decoder_1_out3),
    .out4(decoder_1_out4), .out5(decoder_1_out5), .out6(decoder_1_out6), .out7(decoder_1_out7), .sel(SC));  // open: en
  Decoder #(.select(4)) decoder_2 (
    .out0(decoder_2_out0), .out1(decoder_2_out1), .out2(decoder_2_out2), .out3(decoder_2_out3),
    .out4(decoder_2_out4), .out5(decoder_2_out5), .out6(decoder_2_out6), .out7(decoder_2_out7),
    .out8(decoder_2_out8), .out9(decoder_2_out9), .out10(decoder_2_out10), .out11(decoder_2_out11),
    .out12(decoder_2_out12), .out13(decoder_2_out13), .out14(decoder_2_out14), .out15(decoder_2_out15),
    .sel(IR[17:14]));  // open: en
  and and_1 (p, decoder_1_out3, IR[19], IR[18], decoder_2_out15);
  and and_2 (r_t, decoder_2_out0, decoder_1_out3, IR[19], IR[18]);
  or or_1 (or_1_out, AC[19], AC[18], AC[17], AC[16], AC[15], AC[14], AC[13], AC[12], AC[11], AC[10], AC[8], AC[7], AC[6], AC[5], AC[4], AC[3], AC[2], AC[1], AC[0], AC[9]);
  and and_3 (and_3_out, decoder_1_out5, decoder_2_out6);
  and and_4 (and_4_out, decoder_2_out7, decoder_1_out6);
  and and_5 (and_5_out, ~R, decoder_1_out1);  // AND_Gate
  and and_6 (and_6_out, R, decoder_1_out3);
  and and_7 (and_7_out, decoder_2_out8, ~or_2_out, decoder_1_out6);  // AND_Gate
  and and_8 (and_8_out, IR[6], r_t, ~AC[19]);  // AND_Gate
  and and_9 (and_9_out, IR[5], r_t, AC[19]);
  and and_10 (and_10_out, IR[4], r_t, or_1_out);
  and and_11 (and_11_out, IR[3], r_t, E);
  and and_12 (and_12_out, IR[11], p, FGI);
  and and_13 (and_13_out, IR[10], p, FGO);
  or or_2 (or_2_out, DR[19], DR[18], DR[17], DR[16], DR[15], DR[14], DR[13], DR[12], DR[11], DR[10], DR[8], DR[7], DR[6], DR[5], DR[4], DR[3], DR[2], DR[1], DR[0], DR[9]);
  or or_3 (Load, and_3_out, and_4_out);
  or or_4 (Increment, and_5_out, and_6_out, and_7_out, and_8_out, and_9_out, and_10_out, and_11_out, and_12_out, and_13_out);
  and and_14 (Clear, R, decoder_1_out2);

  // Notes on the sheet:
  //   3x8 decoder
  //   4x8 decoder
  //   D6T5
  //   D7T6
endmodule

module AC (
  input  [19:0] ALU,
  input  Incr,
  input  Clear,
  input  Load,
  input  in_5,
  output [19:0] Output
);

  wire or_1_out;
  wire [19:0] adder_1_out, multiplexer_1_out;

  Adder #(.width(20)) adder_1 (.a(20'h1), .b(Output), .out(adder_1_out));  // open: cin, cout
  Multiplexer #(.width(20), .enable("false")) multiplexer_1 (
    .in0(ALU), .in1(adder_1_out), .out(multiplexer_1_out), .sel(Incr));
  or or_1 (or_1_out, Incr, Load);
  Register #(.width(20), .trigger("high")) register_1 (
    .D(multiplexer_1_out), .en(or_1_out), .Q(Output), .clk(in_5), .clr(Clear));
endmodule

module AC_control (
  input  [19:0] IR,
  input  [2:0] SC,
  output Load,
  output Clear,
  output Increment
);

  wire and_1_out, and_2_out, and_3_out, and_4_out, and_5_out, and_6_out, and_7_out, and_8_out, and_9_out,
       and_10_out, decoder_1_out0, decoder_1_out1, decoder_1_out2, decoder_1_out3, decoder_1_out4,
       decoder_1_out5, decoder_1_out6, decoder_1_out7, decoder_2_out0, decoder_2_out1, decoder_2_out2,
       decoder_2_out3, decoder_2_out4, decoder_2_out5, decoder_2_out6, decoder_2_out7, decoder_2_out8,
       decoder_2_out9, decoder_2_out10, decoder_2_out11, decoder_2_out12, decoder_2_out13, decoder_2_out14,
       decoder_2_out15, p, r;

  Decoder #(.select(3)) decoder_1 (
    .out0(decoder_1_out0), .out1(decoder_1_out1), .out2(decoder_1_out2), .out3(decoder_1_out3),
    .out4(decoder_1_out4), .out5(decoder_1_out5), .out6(decoder_1_out6), .out7(decoder_1_out7), .sel(SC));  // open: en
  Decoder #(.select(4)) decoder_2 (
    .out0(decoder_2_out0), .out1(decoder_2_out1), .out2(decoder_2_out2), .out3(decoder_2_out3),
    .out4(decoder_2_out4), .out5(decoder_2_out5), .out6(decoder_2_out6), .out7(decoder_2_out7),
    .out8(decoder_2_out8), .out9(decoder_2_out9), .out10(decoder_2_out10), .out11(decoder_2_out11),
    .out12(decoder_2_out12), .out13(decoder_2_out13), .out14(decoder_2_out14), .out15(decoder_2_out15),
    .sel(IR[17:14]));  // open: en
  and and_1 (and_1_out, decoder_2_out0, decoder_1_out5);
  and and_2 (and_2_out, decoder_2_out1, decoder_1_out5);
  and and_3 (and_3_out, decoder_2_out2, decoder_1_out5);
  and and_4 (and_4_out, decoder_2_out3, decoder_1_out5);
  and and_5 (and_5_out, decoder_2_out4, decoder_1_out5);
  and and_6 (and_6_out, decoder_2_out9, decoder_1_out6);
  and and_7 (and_7_out, IR[11], r);
  and and_8 (and_8_out, IR[9], r);
  and and_9 (and_9_out, IR[8], r);
  and and_10 (and_10_out, IR[13], p);
  and and_11 (p, decoder_1_out3, IR[19], IR[18], decoder_2_out15);
  and and_12 (r, decoder_2_out0, decoder_1_out3, IR[19], IR[18]);
  or or_1 (Load, and_5_out, and_1_out, and_2_out, and_3_out, and_4_out, and_6_out, and_7_out, and_8_out, and_9_out, and_10_out);
  and and_13 (Clear, IR[13], r);
  and and_14 (Increment, IR[7], p);

  // Notes on the sheet:
  //   3x8 decoder
  //   4x8 decoder
endmodule

module AR (
  input  [19:0] Common_Bus,
  input  Clear,
  input  Load,
  input  INcrement,
  input  Clk,
  output [19:0] OUT
);

  wire or_1_out;
  wire [13:0] adder_1_out, multiplexer_1_out;

  Multiplexer #(.width(14)) multiplexer_1 (
    .in0(Common_Bus[13:0]), .in1(adder_1_out), .out(multiplexer_1_out), .sel(INcrement));  // open: en
  or or_1 (or_1_out, INcrement, Load);
  Register #(.width(14), .trigger("high")) register_1 (
    .D(multiplexer_1_out), .en(or_1_out), .Q(OUT[13:0]), .clk(Clk), .clr(Clear));
  Adder #(.width(14)) adder_1 (.a(14'h1), .b(OUT[13:0]), .out(adder_1_out));  // open: cin, cout

  assign OUT[19:14] = {6{1'b0}};
endmodule

module AR_control (
  input  [19:0] IR,
  input  R,
  input  [2:0] SC,
  output Load,
  output Clear,
  output Increment
);

  wire and_1_out, and_2_out, and_3_out, decoder_1_out0, decoder_1_out1, decoder_1_out2, decoder_1_out3,
       decoder_1_out4, decoder_1_out5, decoder_1_out6, decoder_1_out7, decoder_2_out0, decoder_2_out1,
       decoder_2_out2, decoder_2_out3, decoder_2_out4, decoder_2_out5, decoder_2_out6, decoder_2_out7,
       decoder_2_out8, decoder_2_out9, decoder_2_out10, decoder_2_out11, decoder_2_out12, decoder_2_out13,
       decoder_2_out14, decoder_2_out15;

  Decoder #(.select(3)) decoder_1 (
    .out0(decoder_1_out0), .out1(decoder_1_out1), .out2(decoder_1_out2), .out3(decoder_1_out3),
    .out4(decoder_1_out4), .out5(decoder_1_out5), .out6(decoder_1_out6), .out7(decoder_1_out7), .sel(SC));  // open: en
  Decoder #(.select(4)) decoder_2 (
    .out0(decoder_2_out0), .out1(decoder_2_out1), .out2(decoder_2_out2), .out3(decoder_2_out3),
    .out4(decoder_2_out4), .out5(decoder_2_out5), .out6(decoder_2_out6), .out7(decoder_2_out7),
    .out8(decoder_2_out8), .out9(decoder_2_out9), .out10(decoder_2_out10), .out11(decoder_2_out11),
    .out12(decoder_2_out12), .out13(decoder_2_out13), .out14(decoder_2_out14), .out15(decoder_2_out15),
    .sel(IR[17:14]));  // open: en
  and and_1 (and_1_out, ~R, decoder_1_out0);  // AND_Gate
  and and_2 (and_2_out, ~decoder_2_out0, ~decoder_2_out15, decoder_1_out3, IR[18], ~IR[19]);  // AND_Gate
  and and_3 (and_3_out, ~R, decoder_1_out2);  // AND_Gate
  and and_4 (Clear, R, decoder_1_out1);
  and and_5 (Increment, decoder_2_out7, decoder_1_out5);
  or or_1 (Load, and_1_out, and_2_out, and_3_out);
endmodule

module DR (
  input  [19:0] CBS_Mockup,
  input  Incr,
  input  Load,
  input  in_4,
  output [19:0] out_5
);

  wire button_1_out, or_1_out;
  wire [19:0] adder_1_out, multiplexer_1_out;

  or or_1 (or_1_out, Load, Incr);
  Multiplexer #(.width(20), .enable("false")) multiplexer_1 (
    .in0(CBS_Mockup), .in1(adder_1_out), .out(multiplexer_1_out), .sel(Incr));
  Adder #(.width(20)) adder_1 (.a(20'h1), .b(out_5), .out(adder_1_out));  // open: cin, cout
  Button button_1 (.out(button_1_out));
  Register #(.width(20), .trigger("high")) DR (
    .D(multiplexer_1_out), .en(or_1_out), .Q(out_5), .clk(in_4), .clr(button_1_out));
endmodule

// DR Control
module DR_control (
  input  [19:0] IR,
  input  [2:0] SC,
  output Load,
  output Increment
);

  wire and_1_out, and_2_out, and_3_out, and_4_out, decoder_1_out0, decoder_1_out1, decoder_1_out2,
       decoder_1_out3, decoder_1_out4, decoder_1_out5, decoder_1_out6, decoder_1_out7, decoder_2_out0,
       decoder_2_out1, decoder_2_out2, decoder_2_out3, decoder_2_out4, decoder_2_out5, decoder_2_out6,
       decoder_2_out7, decoder_2_out8, decoder_2_out9, decoder_2_out10, decoder_2_out11, decoder_2_out12,
       decoder_2_out13, decoder_2_out14, decoder_2_out15;

  Decoder #(.select(3)) decoder_1 (
    .out0(decoder_1_out0), .out1(decoder_1_out1), .out2(decoder_1_out2), .out3(decoder_1_out3),
    .out4(decoder_1_out4), .out5(decoder_1_out5), .out6(decoder_1_out6), .out7(decoder_1_out7), .sel(SC));  // open: en
  Decoder #(.select(4)) decoder_2 (
    .out0(decoder_2_out0), .out1(decoder_2_out1), .out2(decoder_2_out2), .out3(decoder_2_out3),
    .out4(decoder_2_out4), .out5(decoder_2_out5), .out6(decoder_2_out6), .out7(decoder_2_out7),
    .out8(decoder_2_out8), .out9(decoder_2_out9), .out10(decoder_2_out10), .out11(decoder_2_out11),
    .out12(decoder_2_out12), .out13(decoder_2_out13), .out14(decoder_2_out14), .out15(decoder_2_out15),
    .sel(IR[17:14]));  // open: en
  and and_1 (and_1_out, ~decoder_2_out0, ~decoder_2_out15, decoder_1_out3, ~IR[19], ~IR[18]);  // AND_Gate
  and and_2 (and_2_out, ~decoder_2_out0, ~decoder_2_out15, decoder_1_out4, ~IR[19], IR[18]);  // AND_Gate
  and and_3 (and_3_out, ~decoder_2_out0, ~decoder_2_out15, decoder_1_out3, IR[19], ~IR[18]);  // AND_Gate
  and and_4 (and_4_out, decoder_2_out9, decoder_1_out6);
  and and_5 (Increment, decoder_2_out8, decoder_1_out5);
  or or_1 (Load, and_1_out, and_2_out, and_3_out, and_4_out);
endmodule

module IR (
  input  [19:0] CBS_Mockup,
  input  Load,
  input  in_3,
  output [19:0] out_4
);

  wire button_1_out;

  Button button_1 (.out(button_1_out));
  Register #(.width(20), .trigger("high")) IR (.D(CBS_Mockup), .en(Load), .Q(out_4), .clk(in_3), .clr(button_1_out));
endmodule

module IR_control (
  input  [2:0] SC,
  input  R,
  output Load
);

  wire decoder_1_out0, decoder_1_out1, decoder_1_out2, decoder_1_out3, decoder_1_out4, decoder_1_out5,
       decoder_1_out6, decoder_1_out7;

  Decoder #(.select(3)) decoder_1 (
    .out0(decoder_1_out0), .out1(decoder_1_out1), .out2(decoder_1_out2), .out3(decoder_1_out3),
    .out4(decoder_1_out4), .out5(decoder_1_out5), .out6(decoder_1_out6), .out7(decoder_1_out7), .sel(SC));  // open: en
  and and_1 (Load, ~R, decoder_1_out1);  // AND_Gate
endmodule

module ALU_Control (
  input  [19:0] in_1,
  input  [2:0] SC,
  output [3:0] out_3
);

  wire ADD_out, AND_4_out, and_5_out, and_6_out, COM, decoder_1_out0, decoder_1_out1, decoder_1_out2,
       decoder_1_out3, decoder_1_out4, decoder_1_out5, decoder_1_out6, decoder_1_out7, decoder_2_out0,
       decoder_2_out1, decoder_2_out2, decoder_2_out3, decoder_2_out4, decoder_2_out5, decoder_2_out6,
       decoder_2_out7, decoder_2_out8, decoder_2_out9, decoder_2_out10, decoder_2_out11, decoder_2_out12,
       decoder_2_out13, decoder_2_out14, decoder_2_out15, DR_out, INPR, not_1_out, or_2_out, OR_out, p, r,
       SHL, SHR, SUB_out;

  Decoder #(.select(3), .enable("false")) decoder_1 (
    .out0(decoder_1_out0), .out1(decoder_1_out1), .out2(decoder_1_out2), .out3(decoder_1_out3),
    .out4(decoder_1_out4), .out5(decoder_1_out5), .out6(decoder_1_out6), .out7(decoder_1_out7), .sel(SC));
  Decoder #(.select(4), .enable("false")) decoder_2 (
    .out0(decoder_2_out0), .out1(decoder_2_out1), .out2(decoder_2_out2), .out3(decoder_2_out3),
    .out4(decoder_2_out4), .out5(decoder_2_out5), .out6(decoder_2_out6), .out7(decoder_2_out7),
    .out8(decoder_2_out8), .out9(decoder_2_out9), .out10(decoder_2_out10), .out11(decoder_2_out11),
    .out12(decoder_2_out12), .out13(decoder_2_out13), .out14(decoder_2_out14), .out15(decoder_2_out15),
    .sel(in_1[17:14]));
  and and_1 (r, decoder_2_out0, in_1[18], in_1[19], decoder_1_out3);
  and and_2 (p, decoder_2_out15, in_1[18], in_1[19], decoder_1_out3);
  and and_3 (INPR, p, in_1[13]);
  and AND_4 (AND_4_out, decoder_1_out5, decoder_2_out0);
  and OR (OR_out, decoder_1_out5, decoder_2_out1);
  and ADD (ADD_out, decoder_1_out5, decoder_2_out2);
  and SUB (SUB_out, decoder_1_out5, decoder_2_out3);
  and and_5 (and_5_out, decoder_1_out5, decoder_2_out4);
  and and_6 (and_6_out, decoder_1_out6, decoder_2_out9);
  and and_7 (SHL, in_1[8], r);
  or DR (DR_out, and_5_out, and_6_out);
  and and_8 (SHR, in_1[9], r);
  and and_9 (COM, in_1[11], r);
  not not_1 (not_1_out, or_2_out);
  or or_2 (or_2_out, COM, SHR, AND_4_out, OR_out, SUB_out, DR_out, SHL, COM, ADD_out);
  Priority_Encoder #(.select(4)) priority_encoder_1 (
    .in0(not_1_out), .in1(AND_4_out), .in2(OR_out), .in3(ADD_out), .in4(SUB_out), .in5(DR_out), .in6(INPR),
    .in7(COM), .in8(SHR), .in9(SHL), .in10(1'b0), .in11(1'b0), .in12(1'b0), .in13(1'b0), .in14(1'b0),
    .in15(1'b0), .out(out_3));  // open: gs, en_out, en_in
endmodule

// ALU
module _20_bit_ALU (
  input  [19:0] AC,
  input  [2:0] SC,
  input  [19:0] IR,
  input  [19:0] DR,
  input  [9:0] INPR,
  input  Carry_in,
  output C_out,
  output [19:0] AC_input
);

  wire button_1_out;
  wire [3:0] alu_control_1_out_3;
  wire [19:0] adder_1_out, adder_2_out, adder_3_out, and_1_out, and_2_out, and_3_out, and_4_out, and_5_out,
       and_6_out, and_7_out, and_8_out, and_9_out, and_10_out, demultiplexer_1_out0, demultiplexer_1_out1,
       demultiplexer_1_out2, demultiplexer_1_out3, demultiplexer_1_out4, demultiplexer_1_out5,
       demultiplexer_1_out6, demultiplexer_1_out7, demultiplexer_1_out8, demultiplexer_1_out9, not_1_out,
       not_2_out, or_1_out, or_2_out, shifter_1_out, shifter_2_out;

  Demultiplexer #(.select(4), .width(20), .enable("false")) demultiplexer_1 (
    .out0(demultiplexer_1_out0), .out1(demultiplexer_1_out1), .out2(demultiplexer_1_out2),
    .out3(demultiplexer_1_out3), .out4(demultiplexer_1_out4), .out5(demultiplexer_1_out5),
    .out6(demultiplexer_1_out6), .out7(demultiplexer_1_out7), .out8(demultiplexer_1_out8),
    .out9(demultiplexer_1_out9), .in({20{1'b1}}), .sel(alu_control_1_out_3));  // open: out10, out11, out12, out13, out14, out15
  ALU_Control alu_control_1 (.SC(SC), .in_1(IR), .out_3(alu_control_1_out_3));
  Shifter #(.width(20), .shift("rr")) shifter_1 (.in(AC_input), .\dist (5'b00001), .out(shifter_1_out));
  Shifter #(.width(20), .shift("rl")) shifter_2 (.in(AC_input), .\dist (5'b00001), .out(shifter_2_out));
  assign not_1_out = ~DR;  // NOT_Gate not_1, 20 bits wide
  assign not_2_out = ~AC;  // NOT_Gate not_2, 20 bits wide
  assign or_1_out = AC | DR;  // OR_Gate or_1, 20 bits wide
  Adder #(.width(20)) adder_1 (.a(AC), .b(DR), .out(adder_1_out), .cin(Carry_in), .cout(C_out));
  Adder #(.width(20)) adder_2 (.a(20'h1), .b(not_1_out), .out(adder_2_out));  // open: cin, cout
  assign and_1_out = demultiplexer_1_out2 & or_1_out;  // AND_Gate and_1, 20 bits wide
  assign and_2_out = demultiplexer_1_out3 & adder_1_out;  // AND_Gate and_2, 20 bits wide
  assign and_3_out = demultiplexer_1_out4 & adder_3_out;  // AND_Gate and_3, 20 bits wide
  Adder #(.width(20)) adder_3 (.a(AC), .b(adder_2_out), .out(adder_3_out));  // open: cin, cout
  assign and_4_out = demultiplexer_1_out5 & DR;  // AND_Gate and_4, 20 bits wide
  assign and_5_out = demultiplexer_1_out6 & {{10{1'b0}}, INPR};  // AND_Gate and_5, 20 bits wide
  assign and_6_out = demultiplexer_1_out7 & not_2_out;  // AND_Gate and_6, 20 bits wide
  assign and_7_out = demultiplexer_1_out8 & shifter_1_out;  // AND_Gate and_7, 20 bits wide
  assign and_8_out = demultiplexer_1_out9 & shifter_2_out;  // AND_Gate and_8, 20 bits wide
  assign and_9_out = AC & demultiplexer_1_out0;  // AND_Gate and_9, 20 bits wide
  assign and_10_out = demultiplexer_1_out1 & AC & DR;  // AND_Gate and_10, 20 bits wide
  assign or_2_out = and_9_out | and_10_out | and_1_out | and_2_out | and_3_out | and_5_out | and_6_out | and_7_out | and_8_out | and_4_out;  // OR_Gate or_2, 20 bits wide
  Register #(.width(20), .trigger("high")) register_1 (
    .D(or_2_out), .Q(AC_input), .clk(1'b1), .clr(button_1_out));  // open: en
  Button button_1 (.out(button_1_out));

  // Notes on the sheet:
  //   Right Shifter
  //   Left shifter
  //   AND
  //   OR
  //   ADD
  //   SUB
  //   DR
  //   INPR
  //   COM
  //   SHR
  //   SHL
endmodule

// Tiiming decoder
module Timing_decoder (
  input  Counter_Input,
  output out_2,
  output out_3,
  output out_4,
  output out_5,
  output out_6,
  output out_7,
  output out_8,
  output out_9
);

  wire button_1_out, clock_1_out;
  wire [2:0] counter_1_q;

  Clock clock_1 (.out(clock_1_out));
  Counter #(.width(3), .max('h7)) counter_1 (
    .load(Counter_Input), .Q(counter_1_q), .clk(clock_1_out), .clr(button_1_out));  // open: D, count, carry
  Button button_1 (.out(button_1_out));
  Decoder #(.select(3)) decoder_1 (
    .out0(out_2), .out1(out_3), .out2(out_4), .out3(out_5), .out4(out_6), .out5(out_7), .out6(out_8),
    .out7(out_9), .sel(counter_1_q));  // open: en
endmodule

// BUS Control
module Bus_Control (
  input  [19:0] IR,
  input  R,
  input  [2:0] SC,
  output [2:0] out_4
);

  wire and_1_out, and_2_out, and_3_out, and_4_out, and_5_out, and_6_out, and_7_out, and_8_out, and_9_out,
       and_10_out, and_11_out, and_12_out, and_13_out, and_14_out, and_15_out, and_17_out, and_18_out,
       and_19_out, and_20_out, and_21_out, decoder_1_out0, decoder_1_out1, decoder_1_out2, decoder_1_out3,
       decoder_1_out4, decoder_1_out5, decoder_1_out6, decoder_1_out7, decoder_2_out0, decoder_2_out1,
       decoder_2_out2, decoder_2_out3, decoder_2_out4, decoder_2_out5, decoder_2_out6, decoder_2_out7,
       decoder_2_out8, decoder_2_out9, decoder_2_out10, decoder_2_out11, decoder_2_out12, decoder_2_out13,
       decoder_2_out14, decoder_2_out15, or_1_out, or_2_out, or_3_out, or_4_out, or_5_out, or_6_out, p;

  Decoder #(.select(3)) decoder_1 (
    .out0(decoder_1_out0), .out1(decoder_1_out1), .out2(decoder_1_out2), .out3(decoder_1_out3),
    .out4(decoder_1_out4), .out5(decoder_1_out5), .out6(decoder_1_out6), .out7(decoder_1_out7), .sel(SC));  // open: en
  Decoder #(.select(4)) decoder_2 (
    .out0(decoder_2_out0), .out1(decoder_2_out1), .out2(decoder_2_out2), .out3(decoder_2_out3),
    .out4(decoder_2_out4), .out5(decoder_2_out5), .out6(decoder_2_out6), .out7(decoder_2_out7),
    .out8(decoder_2_out8), .out9(decoder_2_out9), .out10(decoder_2_out10), .out11(decoder_2_out11),
    .out12(decoder_2_out12), .out13(decoder_2_out13), .out14(decoder_2_out14), .out15(decoder_2_out15),
    .sel(IR[17:14]));  // open: en
  and and_1 (and_1_out, decoder_2_out6, decoder_1_out5);
  and and_2 (and_2_out, decoder_2_out7, decoder_1_out6);
  and and_3 (and_3_out, ~R, decoder_1_out0);  // AND_Gate
  and and_4 (and_4_out, R, decoder_1_out1);
  and and_5 (and_5_out, decoder_2_out7, decoder_1_out5);
  and and_6 (and_6_out, decoder_2_out4, decoder_1_out5);
  and and_7 (and_7_out, decoder_2_out8, decoder_1_out6);
  and and_8 (and_8_out, decoder_2_out9, decoder_1_out6);
  and and_9 (and_9_out, decoder_2_out5, decoder_1_out5);
  and and_10 (and_10_out, decoder_2_out9, decoder_1_out5);
  and and_11 (and_11_out, IR[12], p);
  and and_12 (and_12_out, ~R, decoder_1_out2);  // AND_Gate
  and and_13 (and_13_out, R, decoder_1_out2);
  and and_14 (and_14_out, decoder_2_out9, decoder_1_out6);
  and and_15 (and_15_out, ~R, decoder_1_out1);  // AND_Gate
  and and_16 (p, decoder_1_out3, IR[19], IR[18], decoder_2_out15);
  and and_17 (and_17_out, ~decoder_2_out0, ~decoder_2_out15, decoder_1_out3, IR[19], ~IR[18]);  // AND_Gate
  and and_18 (and_18_out, ~decoder_2_out0, ~decoder_2_out15, decoder_1_out3, ~IR[19], ~IR[18]);  // AND_Gate
  and and_19 (and_19_out, ~decoder_2_out0, ~decoder_2_out15, decoder_1_out3, ~IR[19], IR[18]);  // AND_Gate
  and and_20 (and_20_out, ~decoder_2_out0, ~decoder_2_out15, decoder_1_out4, ~IR[19], IR[18]);  // AND_Gate
  or or_1 (or_1_out, and_6_out, and_7_out, and_8_out);
  or or_2 (or_2_out, and_9_out, and_10_out, and_11_out);
  or or_3 (or_3_out, and_13_out, and_14_out);
  or or_4 (or_4_out, and_17_out, and_1_out, and_2_out);
  or or_5 (or_5_out, and_3_out, and_4_out, and_5_out);
  and and_21 (and_21_out, ~or_4_out, ~or_5_out, ~or_1_out, ~or_2_out, ~and_12_out, ~or_3_out, ~or_6_out);  // AND_Gate
  or or_6 (or_6_out, and_15_out, and_18_out, and_19_out, and_20_out);
  Priority_Encoder priority_encoder_1 (
    .in0(and_21_out), .in1(or_4_out), .in2(or_5_out), .in3(or_1_out), .in4(or_2_out), .in5(and_12_out),
    .in6(or_3_out), .in7(or_6_out), .out(out_4));  // open: en_in, gs, en_out
endmodule

module Final (
  input  [9:0] INPR,
  output [19:0] out_2,
  output [2:0] out_3,
  output [2:0] out_4,
  output out_5,
  output out_6,
  output [19:0] out_7
);

  wire ac_control_1_clear, ac_control_1_increment, ac_control_1_load, and_1_out, ar_control_1_clear,
       ar_control_1_increment, ar_control_1_load, Carry_Out, Clock_out, dr_control_1_increment,
       dr_control_1_load, fgi_flip_flop_1_fgi_value, fgo_flip_flop_1_fgo_value, I0, I1,
       ien_flip_flop_1_ien_value, ir_control_1_load, j_k_ff_1_q, memory_control_1_read,
       memory_control_1_write, pc_control_1_clear, pc_control_1_increment, pc_control_1_load,
       s_flip_flop_control_1_k, tr_control_1_load;
  wire [3:0] ir_1_out_4, ir_1_out_4_2, ir_1_out_4_3, ir_1_out_4_4, ir_1_out_4_5;
  wire [13:0] AR;
  wire [19:0] AC, dr_1_out_5, pc_1_out, ram_1_data, tr_1_output;
  wire [19:14] ar_1_out;

  Clock Clock (.out(Clock_out));
  S_Flip_flop_control s_flip_flop_control_1 (
    .SC(out_3), .IR({ir_1_out_4_5, ir_1_out_4_4, ir_1_out_4_3, ir_1_out_4_2, ir_1_out_4}),
    .K(s_flip_flop_control_1_k), .I0(I0), .I1(I1));
  J_K_Flip_Flop j_k_ff_1 (
    .J(1'b0), .clk(Clock_out), .K(s_flip_flop_control_1_k), .Q(j_k_ff_1_q));  // open: Qn, preset, en, reset
  and and_1 (and_1_out, j_k_ff_1_q, Clock_out);
  E_Flip_flop e_flip_flop_1 (
    .Cout(Carry_Out), .I1(I1), .I0(I0), .SC(out_3),
    .IR({ir_1_out_4_5, ir_1_out_4_4, ir_1_out_4_3, ir_1_out_4_2, ir_1_out_4}), .AC(AC), .E(out_6),
    .clk(and_1_out));
  SC sc_1 (
    .IR({ir_1_out_4_5, ir_1_out_4_4, ir_1_out_4_3, ir_1_out_4_2, ir_1_out_4}), .SC(out_3), .I0(I0), .I1(I1),
    .Clock(and_1_out));
  I1_Flip_flop i1_flip_flop_1 (
    .SC(out_3), .IR({ir_1_out_4_5, ir_1_out_4_4, ir_1_out_4_3, ir_1_out_4_2, ir_1_out_4}), .I1_value(I1),
    .R(out_5), .clk(and_1_out));
  I0_flip_flop i0_flip_flop_1 (
    .SC(out_3), .IR({ir_1_out_4_5, ir_1_out_4_4, ir_1_out_4_3, ir_1_out_4_2, ir_1_out_4}), .I0_Value(I0),
    .R(out_5), .clk(and_1_out));
  FGI_Flip_flop fgi_flip_flop_1 (
    .SC(out_3), .IR({ir_1_out_4_5, ir_1_out_4_4, ir_1_out_4_3, ir_1_out_4_2, ir_1_out_4}),
    .FGI_value(fgi_flip_flop_1_fgi_value), .I1(I1), .I0(I0), .clk(and_1_out));
  FGO_Flip_flop fgo_flip_flop_1 (
    .SC(out_3), .IR({ir_1_out_4_5, ir_1_out_4_4, ir_1_out_4_3, ir_1_out_4_2, ir_1_out_4}),
    .FGO_value(fgo_flip_flop_1_fgo_value), .I0(I0), .I1(I1), .clk(and_1_out));
  IEN_Flip_flop ien_flip_flop_1 (
    .SC(out_3), .IR({ir_1_out_4_5, ir_1_out_4_4, ir_1_out_4_3, ir_1_out_4_2, ir_1_out_4}),
    .IEN_value(ien_flip_flop_1_ien_value), .R(out_5), .I0(I1), .I1(I0), .clk(and_1_out));
  R_Flip_flop r_flip_flop_1 (
    .SC(out_3), .IEN(ien_flip_flop_1_ien_value), .FGI(fgi_flip_flop_1_fgi_value),
    .FGO(fgo_flip_flop_1_fgo_value), .in_5(and_1_out), .R_value(out_5));
  _20_bit_ALU u_20_bit_alu_1 (
    .SC(out_3), .Carry_in(out_6), .IR({ir_1_out_4_5, ir_1_out_4_4, ir_1_out_4_3, ir_1_out_4_2, ir_1_out_4}),
    .AC_input(out_7), .C_out(Carry_Out), .DR(dr_1_out_5), .AC(AC), .INPR(INPR));
  Memory_Control memory_control_1 (
    .R(out_5), .IR({ir_1_out_4_5, ir_1_out_4_4, ir_1_out_4_3, ir_1_out_4_2, ir_1_out_4}),
    .Write(memory_control_1_write), .SC(out_3), .Read(memory_control_1_read));
  IR_control ir_control_1 (.R(out_5), .Load(ir_control_1_load), .SC(out_3));
  AR_control ar_control_1 (
    .Load(ar_control_1_load), .Clear(ar_control_1_clear), .Increment(ar_control_1_increment), .R(out_5),
    .IR({ir_1_out_4_5, ir_1_out_4_4, ir_1_out_4_3, ir_1_out_4_2, ir_1_out_4}), .SC(out_3));
  AR ar_1 (
    .OUT({ar_1_out, AR}), .Load(ar_control_1_load), .Clear(ar_control_1_clear),
    .INcrement(ar_control_1_increment), .Clk(and_1_out), .Common_Bus(out_2));
  PC_control pc_control_1 (
    .IR({ir_1_out_4_5, ir_1_out_4_4, ir_1_out_4_3, ir_1_out_4_2, ir_1_out_4}), .Load(pc_control_1_load),
    .Increment(pc_control_1_increment), .Clear(pc_control_1_clear), .SC(out_3), .R(out_5),
    .FGI(fgi_flip_flop_1_fgi_value), .FGO(fgo_flip_flop_1_fgo_value), .E(out_6), .AC(AC), .DR(dr_1_out_5));
  PC pc_1 (
    .Clk(and_1_out), .Common_Bus(out_2), .OUT(pc_1_out), .Clear(pc_control_1_clear),
    .Load(pc_control_1_load), .Increment(pc_control_1_increment));
  DR_control dr_control_1 (
    .IR({ir_1_out_4_5, ir_1_out_4_4, ir_1_out_4_3, ir_1_out_4_2, ir_1_out_4}), .SC(out_3),
    .Load(dr_control_1_load), .Increment(dr_control_1_increment));
  DR dr_1 (
    .in_4(and_1_out), .out_5(dr_1_out_5), .CBS_Mockup(out_2), .Incr(dr_control_1_increment),
    .Load(dr_control_1_load));
  AC_control ac_control_1 (
    .Clear(ac_control_1_clear), .Increment(ac_control_1_increment), .SC(out_3),
    .IR({ir_1_out_4_5, ir_1_out_4_4, ir_1_out_4_3, ir_1_out_4_2, ir_1_out_4}), .Load(ac_control_1_load));
  AC ac_1 (
    .in_5(and_1_out), .ALU(out_7), .Output(AC), .Incr(ac_control_1_increment), .Load(ac_control_1_load),
    .Clear(ac_control_1_clear));
  IR ir_1 (
    .Load(ir_control_1_load), .in_3(and_1_out),
    .out_4({ir_1_out_4_5, ir_1_out_4_4, ir_1_out_4_3, ir_1_out_4_2, ir_1_out_4}), .CBS_Mockup(out_2));
  TR_control tr_control_1 (
    .SC(out_3), .R(out_5), .IR({ir_1_out_4_5, ir_1_out_4_4, ir_1_out_4_3, ir_1_out_4_2, ir_1_out_4}),
    .Load(tr_control_1_load));
  TR tr_1 (.Load(tr_control_1_load), .in_3(and_1_out), .Output(tr_1_output), .CBS(out_2));
  Bus_Control bus_control_1 (
    .SC(out_3), .IR({ir_1_out_4_5, ir_1_out_4_4, ir_1_out_4_3, ir_1_out_4_2, ir_1_out_4}), .R(out_5),
    .out_4(out_4));
  RAM #(.addrWidth(14), .dataWidth(20), .bus("separate")) ram_1 (
    .addr(AR), .din(out_2), .data(ram_1_data), .str(memory_control_1_write), .clk(and_1_out),
    .ld(memory_control_1_read));  // open: sel, clr
  Multiplexer #(.select(3), .width(20), .enable("false")) multiplexer_1 (
    .in0({20{1'b0}}), .in1({ar_1_out, AR}), .in2(pc_1_out), .in3(dr_1_out_5), .in4(AC),
    .in5({ir_1_out_4_5, ir_1_out_4_4, ir_1_out_4_3, ir_1_out_4_2, ir_1_out_4}), .in6(tr_1_output),
    .in7(ram_1_data), .out(out_2), .sel(out_4));
  Hex_Digit_Display hex_digit_display_1 (.value(out_2[19:16]));  // open: dp
  Hex_Digit_Display hex_digit_display_2 (.value(out_2[15:12]));  // open: dp
  Hex_Digit_Display hex_digit_display_3 (.value(ram_1_data[19:16]));  // open: dp
  Hex_Digit_Display hex_digit_display_4 (.value(ram_1_data[15:12]));  // open: dp
  Hex_Digit_Display hex_digit_display_5 (.value(ar_1_out[19:16]));  // open: dp
  Hex_Digit_Display hex_digit_display_6 (.value({ar_1_out[15:14], AR[13:12]}));  // open: dp
  Hex_Digit_Display hex_digit_display_7 (.value(pc_1_out[19:16]));  // open: dp
  Hex_Digit_Display hex_digit_display_8 (.value(pc_1_out[15:12]));  // open: dp
  Hex_Digit_Display hex_digit_display_9 (.value(dr_1_out_5[15:12]));  // open: dp
  Hex_Digit_Display hex_digit_display_10 (.value(dr_1_out_5[19:16]));  // open: dp
  Hex_Digit_Display hex_digit_display_11 (.value(AC[19:16]));  // open: dp
  Hex_Digit_Display hex_digit_display_12 (.value(ir_1_out_4_4));  // open: dp
  Hex_Digit_Display hex_digit_display_13 (.value(ir_1_out_4_5));  // open: dp
  Hex_Digit_Display hex_digit_display_14 (.value(tr_1_output[19:16]));  // open: dp
  Hex_Digit_Display hex_digit_display_15 (.value(out_2[11:8]));  // open: dp
  Hex_Digit_Display hex_digit_display_16 (.value(out_2[7:4]));  // open: dp
  Hex_Digit_Display hex_digit_display_17 (.value(ram_1_data[11:8]));  // open: dp
  Hex_Digit_Display hex_digit_display_18 (.value(AR[11:8]));  // open: dp
  Hex_Digit_Display hex_digit_display_19 (.value(pc_1_out[11:8]));  // open: dp
  Hex_Digit_Display hex_digit_display_20 (.value(dr_1_out_5[11:8]));  // open: dp
  Hex_Digit_Display hex_digit_display_21 (.value(AC[11:8]));  // open: dp
  Hex_Digit_Display hex_digit_display_22 (.value(AC[15:12]));  // open: dp
  Hex_Digit_Display hex_digit_display_23 (.value(ir_1_out_4_3));  // open: dp
  Hex_Digit_Display hex_digit_display_24 (.value(tr_1_output[15:12]));  // open: dp
  Hex_Digit_Display hex_digit_display_25 (.value(tr_1_output[11:8]));  // open: dp
  Hex_Digit_Display hex_digit_display_26 (.value(out_2[3:0]));  // open: dp
  Hex_Digit_Display hex_digit_display_27 (.value(ram_1_data[3:0]));  // open: dp
  Hex_Digit_Display hex_digit_display_28 (.value(ram_1_data[7:4]));  // open: dp
  Hex_Digit_Display hex_digit_display_29 (.value(AR[3:0]));  // open: dp
  Hex_Digit_Display hex_digit_display_30 (.value(AR[7:4]));  // open: dp
  Hex_Digit_Display hex_digit_display_31 (.value(pc_1_out[7:4]));  // open: dp
  Hex_Digit_Display hex_digit_display_32 (.value(pc_1_out[3:0]));  // open: dp
  Hex_Digit_Display hex_digit_display_33 (.value(dr_1_out_5[7:4]));  // open: dp
  Hex_Digit_Display hex_digit_display_34 (.value(dr_1_out_5[3:0]));  // open: dp
  Hex_Digit_Display hex_digit_display_35 (.value(AC[3:0]));  // open: dp
  Hex_Digit_Display hex_digit_display_36 (.value(AC[7:4]));  // open: dp
  Hex_Digit_Display hex_digit_display_37 (.value(ir_1_out_4_2));  // open: dp
  Hex_Digit_Display hex_digit_display_38 (.value(ir_1_out_4));  // open: dp
  Hex_Digit_Display hex_digit_display_39 (.value(tr_1_output[7:4]));  // open: dp
  Hex_Digit_Display hex_digit_display_40 (.value(tr_1_output[3:0]));  // open: dp

  // Other names for the same wires on the sheet: E = out_6; SC[2:0] = out_3

  // Notes on the sheet:
  //   Common Bus
endmodule

module Memory (
  input  [19:0] AR,
  input  [19:0] CBS_Mockup,
  input  Write,
  input  Clock,
  input  Read,
  output [19:0] Output
);

  RAM #(.addrWidth(14), .dataWidth(20), .bus("separate")) ram_1 (
    .addr(AR[13:0]), .din(CBS_Mockup), .data(Output), .str(Write), .clk(Clock), .ld(Read));  // open: sel, clr
endmodule

module Memory_Control (
  input  [19:0] IR,
  input  R,
  input  [2:0] SC,
  output Write,
  output Read
);

  wire and_1_out, and_2_out, and_3_out, and_4_out, and_5_out, and_6_out, and_7_out, and_8_out,
       decoder_1_out0, decoder_1_out1, decoder_1_out2, decoder_1_out3, decoder_1_out4, decoder_1_out5,
       decoder_1_out6, decoder_1_out7, decoder_2_out0, decoder_2_out1, decoder_2_out2, decoder_2_out3,
       decoder_2_out4, decoder_2_out5, decoder_2_out6, decoder_2_out7, decoder_2_out8, decoder_2_out9,
       decoder_2_out10, decoder_2_out11, decoder_2_out12, decoder_2_out13, decoder_2_out14, decoder_2_out15;

  Decoder #(.select(3), .enable("false")) decoder_1 (
    .out0(decoder_1_out0), .out1(decoder_1_out1), .out2(decoder_1_out2), .out3(decoder_1_out3),
    .out4(decoder_1_out4), .out5(decoder_1_out5), .out6(decoder_1_out6), .out7(decoder_1_out7), .sel(SC));
  Decoder #(.select(4), .enable("false")) decoder_2 (
    .out0(decoder_2_out0), .out1(decoder_2_out1), .out2(decoder_2_out2), .out3(decoder_2_out3),
    .out4(decoder_2_out4), .out5(decoder_2_out5), .out6(decoder_2_out6), .out7(decoder_2_out7),
    .out8(decoder_2_out8), .out9(decoder_2_out9), .out10(decoder_2_out10), .out11(decoder_2_out11),
    .out12(decoder_2_out12), .out13(decoder_2_out13), .out14(decoder_2_out14), .out15(decoder_2_out15),
    .sel(IR[17:14]));
  and and_1 (and_1_out, ~R, decoder_1_out1);  // AND_Gate
  and and_2 (and_2_out, R, decoder_1_out2);
  and and_3 (and_3_out, decoder_1_out5, decoder_2_out5);
  and and_4 (and_4_out, decoder_1_out5, decoder_2_out7);
  and and_5 (and_5_out, decoder_2_out8, decoder_1_out6);
  and and_6 (and_6_out, ~decoder_2_out0, ~decoder_2_out15, decoder_1_out3, ~IR[19], ~IR[18]);  // AND_Gate
  and and_7 (and_7_out, ~decoder_2_out0, ~decoder_2_out15, decoder_1_out4, ~IR[19], IR[18]);  // AND_Gate
  and and_8 (and_8_out, ~decoder_2_out0, ~decoder_2_out15, decoder_1_out3, ~IR[19], IR[18]);  // AND_Gate
  or or_1 (Write, and_2_out, and_3_out, and_4_out, and_5_out);
  or or_2 (Read, and_1_out, and_6_out, and_7_out, and_8_out);

  // Notes on the sheet:
  //   R' T1
  //   D0' D15' T3 I1' I0'
  //   D0' D15' T4 I1' I0
  //   D0' D15 T3 I1' I0
  //   R' T2
  //    D5 T5
  //   D7 T5
  //   D8 T6
endmodule

module TR (
  input  [19:0] CBS,
  input  Load,
  input  in_3,
  output [19:0] Output
);

  wire button_1_out;

  Button button_1 (.out(button_1_out));
  Register #(.width(20)) TR (.D(CBS), .en(Load), .Q(Output), .clk(in_3), .clr(button_1_out));
endmodule

module TR_control (
  input  [2:0] SC,
  input  [19:0] IR,
  input  R,
  output Load
);

  wire and_1_out, and_2_out, decoder_1_out1, decoder_1_out5, decoder_2_out9;

  Decoder #(.select(3), .enable("false")) decoder_1 (
    .out1(decoder_1_out1), .out5(decoder_1_out5), .sel(SC));  // open: out0, out2, out3, out4, out6, out7
  Decoder #(.select(4), .enable("false")) decoder_2 (
    .out9(decoder_2_out9), .sel(IR[17:14]));  // open: out0, out1, out2, out3, out4, out5, out6, out7, out8, out10, out11, out12, out13, out14, out15
  and and_1 (and_1_out, decoder_1_out1, R);
  and and_2 (and_2_out, decoder_1_out5, decoder_2_out9);
  or or_1 (Load, and_1_out, and_2_out);

  // Notes on the sheet:
  //   3x8 decoder
  //   4x16 decoder
endmodule

// I0
module I0_flip_flop (
  input  R,
  input  [19:0] IR,
  input  [2:0] SC,
  input  clk,
  output I0_Value
);

  wire i0_flip_flop_control_1_j, i0_flip_flop_control_1_k;

  I0_Flip_flop_control i0_flip_flop_control_1 (
    .SC(SC), .J(i0_flip_flop_control_1_j), .K(i0_flip_flop_control_1_k), .IR(IR), .R(R));
  J_K_Flip_Flop I0 (
    .J(i0_flip_flop_control_1_j), .clk(clk), .K(i0_flip_flop_control_1_k), .Q(I0_Value));  // open: Qn, preset, en, reset
endmodule

// I0 Flip-flop Control
module I0_Flip_flop_control (
  input  [2:0] SC,
  input  R,
  input  [19:0] IR,
  output J,
  output K
);

  wire and_1_out, decoder_1_out2, not_1_out, not_2_out;

  Decoder #(.select(3), .enable("false")) decoder_1 (
    .out2(decoder_1_out2), .sel(SC));  // open: out0, out1, out3, out4, out5, out6, out7
  not not_1 (not_1_out, R);
  and and_1 (and_1_out, decoder_1_out2, not_1_out);
  not not_2 (not_2_out, IR[18]);
  and and_2 (J, and_1_out, IR[18]);
  and and_3 (K, and_1_out, not_2_out);

  // Notes on the sheet:
  //   3x8 decoder
endmodule

// I1
module I1_Flip_flop (
  input  R,
  input  [19:0] IR,
  input  [2:0] SC,
  input  clk,
  output I1_value
);

  wire i1_flip_flop_control_1_j, i1_flip_flop_control_1_k;

  I1_Flip_flop_control i1_flip_flop_control_1 (
    .SC(SC), .R(R), .J(i1_flip_flop_control_1_j), .K(i1_flip_flop_control_1_k), .IR(IR));
  J_K_Flip_Flop I1 (
    .J(i1_flip_flop_control_1_j), .clk(clk), .K(i1_flip_flop_control_1_k), .Q(I1_value));  // open: Qn, preset, en, reset
endmodule

module I1_Flip_flop_control (
  input  [2:0] SC,
  input  R,
  input  [19:0] IR,
  output J,
  output K
);

  wire and_1_out, decoder_1_out2, not_1_out, not_2_out;

  Decoder #(.select(3), .enable("false")) decoder_1 (
    .out2(decoder_1_out2), .sel(SC));  // open: out0, out1, out3, out4, out5, out6, out7
  not not_1 (not_1_out, R);
  and and_1 (and_1_out, decoder_1_out2, not_1_out);
  not not_2 (not_2_out, IR[19]);
  and and_2 (J, and_1_out, IR[19]);
  and and_3 (K, and_1_out, not_2_out);

  // Notes on the sheet:
  //   3x8 decoder
endmodule

module R_Flip_flop_control (
  input  [2:0] SC,
  input  R,
  input  IEN,
  input  FGI,
  input  FGO,
  output K,
  output J
);

  wire decoder_1_out0, decoder_1_out1, decoder_1_out2, decoder_1_out3, not_1_out, not_2_out, not_3_out,
       or_1_out;

  Decoder #(.select(3), .enable("false")) decoder_1 (
    .out0(decoder_1_out0), .out1(decoder_1_out1), .out2(decoder_1_out2), .out3(decoder_1_out3), .sel(SC));  // open: out4, out5, out6, out7
  not not_1 (not_1_out, decoder_1_out2);
  not not_2 (not_2_out, decoder_1_out1);
  not not_3 (not_3_out, decoder_1_out0);
  or or_1 (or_1_out, FGI, FGO);
  and and_1 (K, R, decoder_1_out3);
  and and_2 (J, not_1_out, not_2_out, not_3_out, IEN, or_1_out);

  // Notes on the sheet:
  //   3x8 decoder
endmodule

// R flip flop
module R_Flip_flop (
  input  FGO,
  input  FGI,
  input  IEN,
  input  [2:0] SC,
  input  in_5,
  output R_value
);

  wire r_flip_flop_control_1_j, r_flip_flop_control_1_k;

  R_Flip_flop_control r_flip_flop_control_1 (
    .SC(SC), .R(R_value), .IEN(IEN), .FGI(FGI), .FGO(FGO), .K(r_flip_flop_control_1_k),
    .J(r_flip_flop_control_1_j));
  J_K_Flip_Flop R (
    .J(r_flip_flop_control_1_j), .clk(in_5), .K(r_flip_flop_control_1_k), .Q(R_value));  // open: Qn, preset, en, reset
endmodule

// IEN
module IEN_Flip_flop (
  input  [19:0] IR,
  input  R,
  input  I1,
  input  [2:0] SC,
  input  I0,
  input  clk,
  output IEN_value
);

  wire ien_flip_flop_control_1_j, ien_flip_flop_control_1_k;

  IEN_Flip_flop_control ien_flip_flop_control_1 (
    .SC(SC), .R(R), .IR(IR), .J(ien_flip_flop_control_1_j), .K(ien_flip_flop_control_1_k), .I0(I0), .I1(I1));
  J_K_Flip_Flop IEN (
    .J(ien_flip_flop_control_1_j), .clk(clk), .K(ien_flip_flop_control_1_k), .Q(IEN_value));  // open: Qn, preset, en, reset
endmodule

module IEN_Flip_flop_control (
  input  [2:0] SC,
  input  [19:0] IR,
  input  I0,
  input  I1,
  input  R,
  output J,
  output K
);

  wire and_3_out, and_4_out, decoder_1_out3, decoder_2_out15, p;

  Decoder #(.select(3), .enable("false")) decoder_1 (
    .out3(decoder_1_out3), .sel(SC));  // open: out0, out1, out2, out4, out5, out6, out7
  Decoder #(.select(4), .enable("false")) decoder_2 (
    .out15(decoder_2_out15), .sel(IR[17:14]));  // open: out0, out1, out2, out3, out4, out5, out6, out7, out8, out9, out10, out11, out12, out13, out14
  and and_1 (p, decoder_2_out15, decoder_1_out3, I0, I1);
  and and_2 (J, IR[9], p);
  and and_3 (and_3_out, p, IR[8]);
  and and_4 (and_4_out, R, decoder_1_out3);
  or or_1 (K, and_3_out, and_4_out);

  // Notes on the sheet:
  //   3x8 decoder
  //   4x16 decoder
endmodule

// FGI
module FGI_Flip_flop (
  input  I0,
  input  [19:0] IR,
  input  I1,
  input  [2:0] SC,
  input  clk,
  output FGI_value
);

  wire fgi_flip_flop_control_1_k;

  FGI_Flip_flop_control fgi_flip_flop_control_1 (.SC(SC), .IR(IR), .K(fgi_flip_flop_control_1_k), .I0(I0), .I1(I1));
  J_K_Flip_Flop FGI (.J(1'b0), .clk(clk), .K(fgi_flip_flop_control_1_k), .Q(FGI_value));  // open: Qn, preset, en, reset
endmodule

module FGI_Flip_flop_control (
  input  [2:0] SC,
  input  [19:0] IR,
  input  I0,
  input  I1,
  output K
);

  wire and_1_out, decoder_1_out3, decoder_2_out15;

  Decoder #(.select(3), .enable("false")) decoder_1 (
    .out3(decoder_1_out3), .sel(SC));  // open: out0, out1, out2, out4, out5, out6, out7
  Decoder #(.select(4), .enable("false")) decoder_2 (
    .out15(decoder_2_out15), .sel(IR[17:14]));  // open: out0, out1, out2, out3, out4, out5, out6, out7, out8, out9, out10, out11, out12, out13, out14
  and and_1 (and_1_out, decoder_2_out15, decoder_1_out3, I0, I1);
  and and_2 (K, IR[13], and_1_out);

  // Notes on the sheet:
  //   3x8 decoder
  //   4x16 decoder
endmodule

// FGO
module FGO_Flip_flop (
  input  I1,
  input  I0,
  input  [19:0] IR,
  input  [2:0] SC,
  input  clk,
  output FGO_value
);

  wire fgo_flip_flop_control_1_k;

  FGO_Flip_flop_control fgo_flip_flop_control_1 (.SC(SC), .IR(IR), .K(fgo_flip_flop_control_1_k), .I0(I0), .I1(I1));
  J_K_Flip_Flop FGO (.J(1'b0), .clk(clk), .K(fgo_flip_flop_control_1_k), .Q(FGO_value));  // open: Qn, preset, en, reset
endmodule

module FGO_Flip_flop_control (
  input  [2:0] SC,
  input  [19:0] IR,
  input  I0,
  input  I1,
  output K
);

  wire and_1_out, decoder_1_out3, decoder_2_out15;

  Decoder #(.select(3), .enable("false")) decoder_1 (
    .out3(decoder_1_out3), .sel(SC));  // open: out0, out1, out2, out4, out5, out6, out7
  Decoder #(.select(4), .enable("false")) decoder_2 (
    .out15(decoder_2_out15), .sel(IR[17:14]));  // open: out0, out1, out2, out3, out4, out5, out6, out7, out8, out9, out10, out11, out12, out13, out14
  and and_1 (and_1_out, decoder_2_out15, decoder_1_out3, I0, I1);
  and and_2 (K, IR[12], and_1_out);

  // Notes on the sheet:
  //   3x8 decoder
  //   4x16 decoder
endmodule

// S
module S_Flip_flop (
  input  I1,
  input  I0,
  input  [19:0] IR,
  input  [2:0] SC,
  input  clk,
  output S_value
);

  wire not_1_out, s_flip_flop_control_1_k;

  S_Flip_flop_control s_flip_flop_control_1 (.SC(SC), .IR(IR), .K(s_flip_flop_control_1_k), .I0(I0), .I1(I1));
  not not_1 (not_1_out, s_flip_flop_control_1_k);
  J_K_Flip_Flop S (.J(not_1_out), .clk(clk), .K(s_flip_flop_control_1_k), .Q(S_value));  // open: Qn, preset, en, reset
endmodule

module S_Flip_flop_control (
  input  [2:0] SC,
  input  [19:0] IR,
  input  I0,
  input  I1,
  output K
);

  wire and_1_out, decoder_1_out3, decoder_2_out0;

  Decoder #(.select(3), .enable("false")) decoder_1 (
    .out3(decoder_1_out3), .sel(SC));  // open: out0, out1, out2, out4, out5, out6, out7
  Decoder #(.select(4), .enable("false")) decoder_2 (
    .out0(decoder_2_out0), .sel(IR[17:14]));  // open: out1, out2, out3, out4, out5, out6, out7, out8, out9, out10, out11, out12, out13, out14, out15
  and and_1 (and_1_out, decoder_2_out0, decoder_1_out3, I0, I1);
  and and_2 (K, IR[2], and_1_out);

  // Notes on the sheet:
  //   3x8 decoder
  //   4x16 decoder
endmodule

// E Flip flop
module E_Flip_flop (
  input  Cout,
  input  [19:0] IR,
  input  I1,
  input  I0,
  input  [19:0] AC,
  input  [2:0] SC,
  input  clk,
  output E
);

  wire e_flip_flop_control_1_j, e_flip_flop_control_1_k;

  E_Flip_flop_control e_flip_flop_control_1 (
    .SC(SC), .AC(AC), .IR(IR), .Cout(Cout), .I0(I0), .I1(I1), .J(e_flip_flop_control_1_j),
    .K(e_flip_flop_control_1_k));
  J_K_Flip_Flop j_k_ff_1 (
    .J(e_flip_flop_control_1_j), .clk(clk), .K(e_flip_flop_control_1_k), .Q(E));  // open: Qn, preset, en, reset
endmodule

module E_Flip_flop_control (
  input  [2:0] SC,
  input  [19:0] IR,
  input  [19:0] AC,
  input  I1,
  input  I0,
  input  Cout,
  output J,
  output K
);

  wire and_2_out, and_3_out, and_4_out, and_5_out, and_6_out, and_7_out, and_8_out, and_9_out, and_10_out,
       and_11_out, and_12_out, decoder_1_out3, decoder_1_out5, decoder_2_out0, decoder_2_out2, not_1_out,
       not_2_out, not_3_out, r;

  Decoder #(.select(3), .enable("false")) decoder_1 (
    .out3(decoder_1_out3), .out5(decoder_1_out5), .sel(SC));  // open: out0, out1, out2, out4, out6, out7
  Decoder #(.select(4), .enable("false")) decoder_2 (
    .out0(decoder_2_out0), .out2(decoder_2_out2), .sel(IR[17:14]));  // open: out1, out3, out4, out5, out6, out7, out8, out9, out10, out11, out12, out13, out14, out15
  and and_1 (r, decoder_2_out0, decoder_1_out3, I0, I1);
  and and_2 (and_2_out, decoder_2_out2, decoder_1_out5);
  and and_3 (and_3_out, r, IR[8]);
  and and_4 (and_4_out, r, IR[9]);
  and and_5 (and_5_out, r, IR[10]);
  and and_6 (and_6_out, r, IR[12]);
  and and_7 (and_7_out, and_4_out, AC[0]);
  or or_1 (J, and_5_out, and_7_out, and_8_out, and_10_out);
  and and_8 (and_8_out, and_3_out, AC[19]);
  not not_1 (not_1_out, AC[19]);
  not not_2 (not_2_out, Cout);
  and and_9 (and_9_out, not_2_out, and_2_out);
  and and_10 (and_10_out, and_2_out, Cout);
  or or_2 (K, and_9_out, and_6_out, and_5_out, and_11_out, and_12_out);
  not not_3 (not_3_out, AC[0]);
  and and_11 (and_11_out, and_4_out, not_3_out);
  and and_12 (and_12_out, and_3_out, not_1_out);

  // Notes on the sheet:
  //   3x8 decoder
  //   4x16 decoder
  //   rB8
  //   rB9
  //   rB10
  //   rB12
  //   D2T5
endmodule

module OUTR_Control (
  input  [2:0] SC,
  input  [19:0] IR,
  output Load
);

  wire decoder_1_out0, decoder_1_out1, decoder_1_out2, decoder_1_out3, decoder_1_out4, decoder_1_out5,
       decoder_1_out6, decoder_1_out7, decoder_2_out0, decoder_2_out1, decoder_2_out2, decoder_2_out3,
       decoder_2_out4, decoder_2_out5, decoder_2_out6, decoder_2_out7, decoder_2_out8, decoder_2_out9,
       decoder_2_out10, decoder_2_out11, decoder_2_out12, decoder_2_out13, decoder_2_out14, decoder_2_out15,
       p;

  Decoder #(.select(3), .enable("false")) decoder_1 (
    .out0(decoder_1_out0), .out1(decoder_1_out1), .out2(decoder_1_out2), .out3(decoder_1_out3),
    .out4(decoder_1_out4), .out5(decoder_1_out5), .out6(decoder_1_out6), .out7(decoder_1_out7), .sel(SC));
  Decoder #(.select(4), .enable("false")) decoder_2 (
    .out0(decoder_2_out0), .out1(decoder_2_out1), .out2(decoder_2_out2), .out3(decoder_2_out3),
    .out4(decoder_2_out4), .out5(decoder_2_out5), .out6(decoder_2_out6), .out7(decoder_2_out7),
    .out8(decoder_2_out8), .out9(decoder_2_out9), .out10(decoder_2_out10), .out11(decoder_2_out11),
    .out12(decoder_2_out12), .out13(decoder_2_out13), .out14(decoder_2_out14), .out15(decoder_2_out15),
    .sel(IR[17:14]));
  and and_1 (p, decoder_2_out15, IR[18], IR[19], decoder_1_out3);
  and and_2 (Load, IR[12], p);

  // Notes on the sheet:
  //   p.B12
  //   D15.I1.I0.T3
endmodule

module OUTR (
  input  [19:0] AC,
  input  [2:0] SC,
  input  [19:0] IR,
  input  Clock,
  output [9:0] Output
);

  wire outr_control_1_load, Reset_out;

  OUTR_Control outr_control_1 (.IR(IR), .Load(outr_control_1_load), .SC(SC));
  Register #(.width(10)) OUTR (.D(AC[9:0]), .en(outr_control_1_load), .Q(Output), .clk(Clock), .clr(Reset_out));
  Button Reset (.out(Reset_out));
endmodule

module SC_Control (
  input  [2:0] SC,
  input  I1,
  input  I0,
  input  [19:0] IR,
  output Clear
);

  wire and_1_out, and_2_out, and_3_out, and_4_out, and_5_out, and_6_out, and_7_out, and_8_out, and_9_out,
       and_10_out, decoder_1_out0, decoder_1_out1, decoder_1_out2, decoder_1_out3, decoder_1_out4,
       decoder_1_out5, decoder_1_out6, decoder_1_out7, decoder_2_out0, decoder_2_out1, decoder_2_out2,
       decoder_2_out3, decoder_2_out4, decoder_2_out5, decoder_2_out6, decoder_2_out7, decoder_2_out8,
       decoder_2_out9, decoder_2_out10, decoder_2_out11, decoder_2_out12, decoder_2_out13, decoder_2_out14,
       decoder_2_out15, p, r;

  Decoder #(.select(3), .enable("false")) decoder_1 (
    .out0(decoder_1_out0), .out1(decoder_1_out1), .out2(decoder_1_out2), .out3(decoder_1_out3),
    .out4(decoder_1_out4), .out5(decoder_1_out5), .out6(decoder_1_out6), .out7(decoder_1_out7), .sel(SC));
  Decoder #(.select(4), .enable("false")) decoder_2 (
    .out0(decoder_2_out0), .out1(decoder_2_out1), .out2(decoder_2_out2), .out3(decoder_2_out3),
    .out4(decoder_2_out4), .out5(decoder_2_out5), .out6(decoder_2_out6), .out7(decoder_2_out7),
    .out8(decoder_2_out8), .out9(decoder_2_out9), .out10(decoder_2_out10), .out11(decoder_2_out11),
    .out12(decoder_2_out12), .out13(decoder_2_out13), .out14(decoder_2_out14), .out15(decoder_2_out15),
    .sel(IR[17:14]));
  and and_1 (and_1_out, decoder_2_out0, decoder_1_out5);
  and and_2 (and_2_out, decoder_2_out1, decoder_1_out5);
  and and_3 (and_3_out, decoder_2_out2, decoder_1_out5);
  and and_4 (and_4_out, decoder_2_out3, decoder_1_out5);
  and and_5 (and_5_out, decoder_2_out4, decoder_1_out5);
  and and_6 (and_6_out, decoder_2_out5, decoder_1_out5);
  and and_7 (and_7_out, decoder_2_out6, decoder_1_out5);
  and and_8 (and_8_out, decoder_2_out7, decoder_1_out6);
  and and_9 (and_9_out, decoder_2_out8, decoder_1_out6);
  and and_10 (and_10_out, decoder_2_out9, decoder_1_out6);
  and and_11 (r, decoder_2_out0, I0, I1, decoder_1_out3);
  and and_12 (p, decoder_2_out15, I0, I1, decoder_1_out3);
  or or_1 (Clear, and_1_out, and_2_out, and_3_out, and_4_out, and_5_out, and_6_out, and_7_out, and_8_out, and_9_out, and_10_out, r, p);

  // Notes on the sheet:
  //   D0.T5
  //   D1.T5
  //   D2.T5
  //   D3.T5
  //   D4.T5
  //   D5.T5
  //   D6.T5
  //   D7.T6
  //   D8.T6
  //   D9.T6
endmodule

module SC (
  input  Clock,
  input  [19:0] IR,
  input  I1,
  input  I0,
  output [2:0] SC
);

  wire not_1_out, sc_control_1_clear;
  wire [2:0] subtractor_1_out;

  SC_Control sc_control_1 (.IR(IR), .Clear(sc_control_1_clear), .SC(subtractor_1_out), .I1(I1), .I0(I0));
  not not_1 (not_1_out, sc_control_1_clear);
  Counter #(.width(3), .max('h7)) u_SC (
    .count(not_1_out), .Q(SC), .clk(Clock), .clr(sc_control_1_clear));  // open: load, D, carry
  Subtractor #(.width(3)) subtractor_1 (.a(SC), .b(3'b001), .out(subtractor_1_out));  // open: bin, bout
endmodule
