// Logisim project Memory_shreyam.circ as structural Verilog: 2 circuits, main circuit Memory
module Memory (
  input  [13:0] AR,
  input  [19:0] IR,
  input  [19:0] CBS_Mockup,
  input  [2:0] SC,
  input  R,
  input  Read,
  output [19:0] Output
);

  wire clock_1_out, memory_control_1_write;

  Memory_Control memory_control_1 (.R(R), .IR(IR), .Write(memory_control_1_write), .SC(SC));
  Clock clock_1 (.out(clock_1_out));
  RAM #(.addrWidth(14), .dataWidth(20), .bus("separate")) ram_1 (
    .addr(AR), .din(CBS_Mockup), .data(Output), .str(memory_control_1_write), .clk(clock_1_out), .ld(Read));  // open: sel, clr

  // Notes on the sheet:
  //   Write
endmodule

module Memory_Control (
  input  [19:0] IR,
  input  [2:0] SC,
  input  R,
  output Write
);

  wire and_1_out, and_2_out, and_3_out, and_4_out, decoder_1_out0, decoder_1_out1, decoder_1_out2,
       decoder_1_out3, decoder_1_out4, decoder_1_out5, decoder_1_out6, decoder_1_out7, decoder_2_out0,
       decoder_2_out1, decoder_2_out2, decoder_2_out3, decoder_2_out4, decoder_2_out5, decoder_2_out6,
       decoder_2_out7, decoder_2_out8, decoder_2_out9, decoder_2_out10, decoder_2_out11, decoder_2_out12,
       decoder_2_out13, decoder_2_out14, decoder_2_out15;

  Decoder #(.select(3), .enable("false")) decoder_1 (
    .out0(decoder_1_out0), .out1(decoder_1_out1), .out2(decoder_1_out2), .out3(decoder_1_out3),
    .out4(decoder_1_out4), .out5(decoder_1_out5), .out6(decoder_1_out6), .out7(decoder_1_out7), .sel(SC));
  Decoder #(.select(4), .enable("false")) decoder_2 (
    .out0(decoder_2_out0), .out1(decoder_2_out1), .out2(decoder_2_out2), .out3(decoder_2_out3),
    .out4(decoder_2_out4), .out5(decoder_2_out5), .out6(decoder_2_out6), .out7(decoder_2_out7),
    .out8(decoder_2_out8), .out9(decoder_2_out9), .out10(decoder_2_out10), .out11(decoder_2_out11),
    .out12(decoder_2_out12), .out13(decoder_2_out13), .out14(decoder_2_out14), .out15(decoder_2_out15),
    .sel(IR[17:14]));
  and and_1 (and_1_out, R, decoder_1_out2);
  and and_2 (and_2_out, decoder_1_out5, decoder_2_out5);
  and and_3 (and_3_out, decoder_1_out5, decoder_2_out7);
  and and_4 (and_4_out, decoder_2_out8, decoder_1_out6);
  or or_1 (Write, and_1_out, and_2_out, and_3_out, and_4_out);
endmodule
