// Logisim project OUTR.circ as structural Verilog: 2 circuits, main circuit OUTR Control
module OUTR_Control (
  input  [2:0] SC,
  input  [19:0] IR,
  output Load
);

  wire decoder_1_out0, decoder_1_out1, decoder_1_out2, decoder_1_out3, decoder_1_out4, decoder_1_out5,
       decoder_1_out6, decoder_1_out7, decoder_2_out0, decoder_2_out1, decoder_2_out2, decoder_2_out3,
       decoder_2_out4, decoder_2_out5, decoder_2_out6, decoder_2_out7, decoder_2_out8, decoder_2_out9,
       decoder_2_out10, decoder_2_out11, decoder_2_out12, decoder_2_out13, decoder_2_out14, decoder_2_out15,
       p;

  Decoder #(.select(3), .enable("false")) decoder_1 (
    .out0(decoder_1_out0), .out1(decoder_1_out1), .out2(decoder_1_out2), .out3(decoder_1_out3),
    .out4(decoder_1_out4), .out5(decoder_1_out5), .out6(decoder_1_out6), .out7(decoder_1_out7), .sel(SC));
  Decoder #(.select(4), .enable("false")) decoder_2 (
    .out0(decoder_2_out0), .out1(decoder_2_out1), .out2(decoder_2_out2), .out3(decoder_2_out3),
    .out4(decoder_2_out4), .out5(decoder_2_out5), .out6(decoder_2_out6), .out7(decoder_2_out7),
    .out8(decoder_2_out8), .out9(decoder_2_out9), .out10(decoder_2_out10), .out11(decoder_2_out11),
    .out12(decoder_2_out12), .out13(decoder_2_out13), .out14(decoder_2_out14), .out15(decoder_2_out15),
    .sel(IR[17:14]));
  and and_1 (p, decoder_2_out15, IR[18], IR[19], decoder_1_out3);
  and and_2 (Load, IR[12], p);

  // Notes on the sheet:
  //   p.B12
  //   D15.I1.I0.T3
endmodule

module OUTR (
  input  [19:0] AC,
  input  [2:0] SC,
  input  [19:0] IR,
  input  Clock,
  output [9:0] Output
);

  wire outr_control_1_load, Reset_out;

  OUTR_Control outr_control_1 (.IR(IR), .Load(outr_control_1_load), .SC(SC));
  Register #(.width(10)) OUTR (.D(AC[9:0]), .en(outr_control_1_load), .Q(Output), .clk(Clock), .clr(Reset_out));
  Button Reset (.out(Reset_out));
endmodule
