// Logisim project SC.circ as structural Verilog: 2 circuits, main circuit SC Control
module SC_Control (
  input  [2:0] SC,
  input  I1,
  input  I0,
  input  [19:0] IR,
  output Clear
);

  wire and_1_out, and_2_out, and_3_out, and_4_out, and_5_out, and_6_out, and_7_out, and_8_out, and_9_out,
       and_10_out, decoder_1_out0, decoder_1_out1, decoder_1_out2, decoder_1_out3, decoder_1_out4,
       decoder_1_out5, decoder_1_out6, decoder_1_out7, decoder_2_out0, decoder_2_out1, decoder_2_out2,
       decoder_2_out3, decoder_2_out4, decoder_2_out5, decoder_2_out6, decoder_2_out7, decoder_2_out8,
       decoder_2_out9, decoder_2_out10, decoder_2_out11, decoder_2_out12, decoder_2_out13, decoder_2_out14,
       decoder_2_out15, p, r;

  Decoder #(.select(3), .enable("false")) decoder_1 (
    .out0(decoder_1_out0), .out1(decoder_1_out1), .out2(decoder_1_out2), .out3(decoder_1_out3),
    .out4(decoder_1_out4), .out5(decoder_1_out5), .out6(decoder_1_out6), .out7(decoder_1_out7), .sel(SC));
  Decoder #(.select(4), .enable("false")) decoder_2 (
    .out0(decoder_2_out0), .out1(decoder_2_out1), .out2(decoder_2_out2), .out3(decoder_2_out3),
    .out4(decoder_2_out4), .out5(decoder_2_out5), .out6(decoder_2_out6), .out7(decoder_2_out7),
    .out8(decoder_2_out8), .out9(decoder_2_out9), .out10(decoder_2_out10), .out11(decoder_2_out11),
    .out12(decoder_2_out12), .out13(decoder_2_out13), .out14(decoder_2_out14), .out15(decoder_2_out15),
    .sel(IR[17:14]));
  and and_1 (and_1_out, decoder_2_out0, decoder_1_out5);
  and and_2 (and_2_out, decoder_2_out1, decoder_1_out5);
  and and_3 (and_3_out, decoder_2_out2, decoder_1_out5);
  and and_4 (and_4_out, decoder_2_out3, decoder_1_out5);
  and and_5 (and_5_out, decoder_2_out4, decoder_1_out5);
  and and_6 (and_6_out, decoder_2_out5, decoder_1_out5);
  and and_7 (and_7_out, decoder_2_out6, decoder_1_out5);
  and and_8 (and_8_out, decoder_2_out7, decoder_1_out6);
  and and_9 (and_9_out, decoder_2_out8, decoder_1_out6);
  and and_10 (and_10_out, decoder_2_out9, decoder_1_out6);
  and and_11 (r, decoder_2_out0, I0, I1, decoder_1_out3);
  and and_12 (p, decoder_2_out15, I0, I1, decoder_1_out3);
  or or_1 (Clear, and_1_out, and_2_out, and_3_out, and_4_out, and_5_out, and_6_out, and_7_out, and_8_out, and_9_out, and_10_out, r, p);

  // Notes on the sheet:
  //   D0.T5
  //   D1.T5
  //   D2.T5
  //   D3.T5
  //   D4.T5
  //   D5.T5
  //   D6.T5
  //   D7.T6
  //   D8.T6
  //   D9.T6
endmodule

module SC (
  input  Clock,
  input  [19:0] IR,
  input  I1,
  input  I0,
  output [2:0] SC
);

  wire not_1_out, sc_control_1_clear;
  wire [2:0] subtractor_1_out;

  SC_Control sc_control_1 (.IR(IR), .Clear(sc_control_1_clear), .SC(subtractor_1_out), .I1(I1), .I0(I0));
  not not_1 (not_1_out, sc_control_1_clear);
  Counter #(.width(3), .max('h7)) u_SC (
    .count(not_1_out), .Q(SC), .clk(Clock), .clr(sc_control_1_clear));  // open: load, D, carry
  Subtractor #(.width(3)) subtractor_1 (.a(SC), .b(3'b001), .out(subtractor_1_out));  // open: bin, bout
endmodule
