// Logisim project ramraj.circ as structural Verilog
module PC (
  input  [19:0] AC,
  input  [19:0] DR,
  input  [19:0] IR,
  input  FGO,
  input  FGI,
  input  R,
  input  E,
  input  [2:0] in_8,
  input  in_9,
  output [13:0] out_10
);

  wire or_1_out, pc_control_1_clear, pc_control_1_increment, pc_control_1_load;
  wire [13:0] adder_1_out, multiplexer_1_out;

  PC_control pc_control_1 (
    .IR(IR), .Load(pc_control_1_load), .Increment(pc_control_1_increment), .Clear(pc_control_1_clear),
    .SC(in_8), .R(R), .FGI(FGI), .FGO(FGO), .E(E), .AC(AC), .DR(DR));
  Multiplexer #(.width(14), .enable("false")) multiplexer_1 (
    .in0(IR[13:0]), .in1(adder_1_out), .out(multiplexer_1_out), .sel(pc_control_1_increment));
  Adder #(.width(14)) adder_1 (.a(14'h1), .b(out_10), .out(adder_1_out));  // open: cin, cout
  or or_1 (or_1_out, pc_control_1_increment, pc_control_1_load);
  Register #(.width(14)) register_1 (
    .D(multiplexer_1_out), .en(or_1_out), .Q(out_10), .clk(in_9), .clr(pc_control_1_clear));
endmodule

// PC Control
module PC_control (
  input  [19:0] IR,
  input  [2:0] SC,
  input  [19:0] AC,
  input  [19:0] DR,
  input  R,
  input  FGI,
  input  FGO,
  input  E,
  output Load,
  output Increment,
  output Clear
);

  wire and_3_out, and_4_out, and_5_out, and_6_out, and_7_out, and_8_out, and_9_out, and_10_out, and_11_out,
       and_12_out, and_13_out, decoder_1_out0, decoder_1_out1, decoder_1_out2, decoder_1_out3,
       decoder_1_out4, decoder_1_out5, decoder_1_out6, decoder_1_out7, decoder_2_out0, decoder_2_out1,
       decoder_2_out2, decoder_2_out3, decoder_2_out4, decoder_2_out5, decoder_2_out6, decoder_2_out7,
       decoder_2_out8, decoder_2_out9, decoder_2_out10, decoder_2_out11, decoder_2_out12, decoder_2_out13,
       decoder_2_out14, decoder_2_out15, or_1_out, or_2_out, p, r_t;

  Decoder #(.select(3)) decoder_1 (
    .out0(decoder_1_out0), .out1(decoder_1_out1), .out2(decoder_1_out2), .out3(decoder_1_out3),
    .out4(decoder_1_out4), .out5(decoder_1_out5), .out6(decoder_1_out6), .out7(decoder_1_out7), .sel(SC));  // open: en
  Decoder #(.select(4)) decoder_2 (
    .out0(decoder_2_out0), .out1(decoder_2_out1), .out2(decoder_2_out2), .out3(decoder_2_out3),
    .out4(decoder_2_out4), .out5(decoder_2_out5), .out6(decoder_2_out6), .out7(decoder_2_out7),
    .out8(decoder_2_out8), .out9(decoder_2_out9), .out10(decoder_2_out10), .out11(decoder_2_out11),
    .out12(decoder_2_out12), .out13(decoder_2_out13), .out14(decoder_2_out14), .out15(decoder_2_out15),
    .sel(IR[17:14]));  // open: en
  and and_1 (p, decoder_1_out3, IR[19], IR[18], decoder_2_out15);
  and and_2 (r_t, decoder_2_out0, decoder_1_out3, IR[19], IR[18]);
  or or_1 (or_1_out, AC[19], AC[18], AC[17], AC[16], AC[15], AC[14], AC[13], AC[12], AC[11], AC[10], AC[8], AC[7], AC[6], AC[5], AC[4], AC[3], AC[2], AC[1], AC[0], AC[9]);
  and and_3 (and_3_out, decoder_1_out5, decoder_2_out6);
  and and_4 (and_4_out, decoder_2_out7, decoder_1_out6);
  and and_5 (and_5_out, ~R, decoder_1_out1);  // AND_Gate
  and and_6 (and_6_out, R, decoder_1_out3);
  and and_7 (and_7_out, decoder_2_out8, ~or_2_out, decoder_1_out6);  // AND_Gate
  and and_8 (and_8_out, IR[6], r_t, ~AC[19]);  // AND_Gate
  and and_9 (and_9_out, IR[5], r_t, AC[19]);
  and and_10 (and_10_out, IR[4], r_t, or_1_out);
  and and_11 (and_11_out, IR[3], r_t, E);
  and and_12 (and_12_out, IR[11], p, FGI);
  and and_13 (and_13_out, IR[10], p, FGO);
  or or_2 (or_2_out, DR[19], DR[18], DR[17], DR[16], DR[15], DR[14], DR[13], DR[12], DR[11], DR[10], DR[8], DR[7], DR[6], DR[5], DR[4], DR[3], DR[2], DR[1], DR[0], DR[9]);
  or or_3 (Load, and_3_out, and_4_out);
  or or_4 (Increment, and_5_out, and_6_out, and_7_out, and_8_out, and_9_out, and_10_out, and_11_out, and_12_out, and_13_out);
  and and_14 (Clear, R, decoder_1_out2);

  // Notes on the sheet:
  //   3x8 decoder
  //   4x8 decoder
  //   D6T5
  //   D7T6
endmodule

module AC (
  input  [19:0] IR,
  input  [2:0] in_2,
  input  [19:0] ALU,
  input  in_4,
  output [19:0] out_5
);

  wire ac_control_1_clear, ac_control_1_increment, ac_control_1_load, or_1_out;
  wire [19:0] adder_1_out, multiplexer_1_out;

  AC_control ac_control_1 (
    .Clear(ac_control_1_clear), .Increment(ac_control_1_increment), .SC(in_2), .IR(IR),
    .Load(ac_control_1_load));
  Adder #(.width(20)) adder_1 (.a(20'h1), .b(out_5), .out(adder_1_out));  // open: cin, cout
  Multiplexer #(.width(20), .enable("false")) multiplexer_1 (
    .in0(ALU), .in1(adder_1_out), .out(multiplexer_1_out), .sel(ac_control_1_load));
  or or_1 (or_1_out, ac_control_1_load, ac_control_1_increment);
  Register #(.width(20)) register_1 (
    .D(multiplexer_1_out), .en(or_1_out), .Q(out_5), .clk(in_4), .clr(ac_control_1_clear));
endmodule

module AC_control (
  input  [19:0] IR,
  input  [2:0] SC,
  output Load,
  output Clear,
  output Increment
);

  wire and_1_out, and_2_out, and_3_out, and_4_out, and_5_out, and_6_out, and_7_out, and_8_out, and_9_out,
       decoder_1_out0, decoder_1_out1, decoder_1_out2, decoder_1_out3, decoder_1_out4, decoder_1_out5,
       decoder_1_out6, decoder_1_out7, decoder_2_out0, decoder_2_out1, decoder_2_out2, decoder_2_out3,
       decoder_2_out4, decoder_2_out5, decoder_2_out6, decoder_2_out7, decoder_2_out8, decoder_2_out9,
       decoder_2_out10, decoder_2_out11, decoder_2_out12, decoder_2_out13, decoder_2_out14, decoder_2_out15,
       p, r;

  Decoder #(.select(3)) decoder_1 (
    .out0(decoder_1_out0), .out1(decoder_1_out1), .out2(decoder_1_out2), .out3(decoder_1_out3),
    .out4(decoder_1_out4), .out5(decoder_1_out5), .out6(decoder_1_out6), .out7(decoder_1_out7), .sel(SC));  // open: en
  Decoder #(.select(4)) decoder_2 (
    .out0(decoder_2_out0), .out1(decoder_2_out1), .out2(decoder_2_out2), .out3(decoder_2_out3),
    .out4(decoder_2_out4), .out5(decoder_2_out5), .out6(decoder_2_out6), .out7(decoder_2_out7),
    .out8(decoder_2_out8), .out9(decoder_2_out9), .out10(decoder_2_out10), .out11(decoder_2_out11),
    .out12(decoder_2_out12), .out13(decoder_2_out13), .out14(decoder_2_out14), .out15(decoder_2_out15),
    .sel(IR[17:14]));  // open: en
  and and_1 (and_1_out, decoder_2_out0, decoder_1_out5);
  and and_2 (and_2_out, decoder_2_out1, decoder_1_out5);
  and and_3 (and_3_out, decoder_2_out2, decoder_1_out5);
  and and_4 (and_4_out, decoder_2_out3, decoder_1_out5);
  and and_5 (and_5_out, decoder_2_out4, decoder_1_out5);
  and and_6 (and_6_out, decoder_2_out9, decoder_1_out6);
  and and_7 (and_7_out, IR[9], r);
  and and_8 (and_8_out, IR[8], r);
  and and_9 (and_9_out, IR[11], p);
  and and_10 (p, decoder_1_out3, IR[19], IR[18], decoder_2_out15);
  and and_11 (r, decoder_2_out0, decoder_1_out3, IR[19], IR[18]);
  or or_1 (Load, and_1_out, and_2_out, and_3_out, and_4_out, and_5_out, and_6_out, and_7_out, and_8_out, and_9_out);
  and and_12 (Clear, IR[13], r);
  and and_13 (Increment, IR[7], p);

  // Notes on the sheet:
  //   3x8 decoder
  //   4x8 decoder
endmodule

module AR (
  input  [19:0] IR,
  input  in_2,
  input  in_3,
  output [13:0] Bus_OUT
);

  wire ar_control_1_clear, ar_control_1_increment, ar_control_1_load, clock_1_out, or_1_out;
  wire [13:0] adder_1_out, multiplexer_1_out;

  Clock clock_1 (.out(clock_1_out));
  AR_control ar_control_1 (
    .Load(ar_control_1_load), .Clear(ar_control_1_clear), .Increment(ar_control_1_increment), .R(in_3),
    .IR(IR), .Counter_Input(in_2));
  Multiplexer #(.width(14)) multiplexer_1 (
    .in0(IR[13:0]), .in1(adder_1_out), .out(multiplexer_1_out), .sel(ar_control_1_increment));  // open: en
  or or_1 (or_1_out, ar_control_1_increment, ar_control_1_load);
  Register #(.width(14)) register_1 (
    .D(multiplexer_1_out), .en(or_1_out), .Q(Bus_OUT), .clk(clock_1_out), .clr(ar_control_1_clear));
  Adder #(.width(14)) adder_1 (.a(14'h1), .b(Bus_OUT), .out(adder_1_out));  // open: cin, cout
endmodule

module AR_control (
  input  Counter_Input,
  input  [19:0] IR,
  input  R,
  output Load,
  output Clear,
  output Increment
);

  wire and_1_out, and_2_out, and_3_out, button_1_out, clock_1_out, decoder_1_out0, decoder_1_out1,
       decoder_1_out2, decoder_1_out3, decoder_1_out4, decoder_1_out5, decoder_1_out6, decoder_1_out7,
       decoder_2_out0, decoder_2_out1, decoder_2_out2, decoder_2_out3, decoder_2_out4, decoder_2_out5,
       decoder_2_out6, decoder_2_out7, decoder_2_out8, decoder_2_out9, decoder_2_out10, decoder_2_out11,
       decoder_2_out12, decoder_2_out13, decoder_2_out14, decoder_2_out15;
  wire [2:0] counter_1_q;

  Clock clock_1 (.out(clock_1_out));
  Counter #(.width(3), .max('h7)) counter_1 (
    .load(Counter_Input), .Q(counter_1_q), .clk(clock_1_out), .clr(button_1_out));  // open: D, count, carry
  Button button_1 (.out(button_1_out));
  Decoder #(.select(3)) decoder_1 (
    .out0(decoder_1_out0), .out1(decoder_1_out1), .out2(decoder_1_out2), .out3(decoder_1_out3),
    .out4(decoder_1_out4), .out5(decoder_1_out5), .out6(decoder_1_out6), .out7(decoder_1_out7),
    .sel(counter_1_q));  // open: en
  Decoder #(.select(4)) decoder_2 (
    .out0(decoder_2_out0), .out1(decoder_2_out1), .out2(decoder_2_out2), .out3(decoder_2_out3),
    .out4(decoder_2_out4), .out5(decoder_2_out5), .out6(decoder_2_out6), .out7(decoder_2_out7),
    .out8(decoder_2_out8), .out9(decoder_2_out9), .out10(decoder_2_out10), .out11(decoder_2_out11),
    .out12(decoder_2_out12), .out13(decoder_2_out13), .out14(decoder_2_out14), .out15(decoder_2_out15),
    .sel(IR[17:14]));  // open: en
  and and_1 (and_1_out, ~R, decoder_1_out0);  // AND_Gate
  and and_2 (and_2_out, ~decoder_2_out0, ~decoder_2_out15, decoder_1_out3, ~IR[18], ~IR[19]);  // AND_Gate
  and and_3 (and_3_out, ~R, decoder_1_out2);  // AND_Gate
  and and_4 (Clear, R, decoder_1_out1);
  and and_5 (Increment, decoder_2_out7, decoder_1_out5);
  or or_1 (Load, and_1_out, and_2_out, and_3_out);
endmodule

module DR (
  input  [19:0] in_1,
  input  [19:0] CBS_Mockup,
  input  in_3,
  input  in_4,
  output [19:0] out_5
);

  wire button_1_out, dr_control_1_increment, dr_control_1_load, or_1_out;
  wire [19:0] adder_1_out, multiplexer_1_out;

  DR_control dr_control_1 (.IR(in_1), .in_2(in_3), .Load(dr_control_1_load), .Increment(dr_control_1_increment));
  or or_1 (or_1_out, dr_control_1_load, dr_control_1_increment);
  Multiplexer #(.width(20), .enable("false")) multiplexer_1 (
    .in0(CBS_Mockup), .in1(adder_1_out), .out(multiplexer_1_out), .sel(dr_control_1_increment));
  Adder #(.width(20)) adder_1 (.a(20'h1), .b(out_5), .out(adder_1_out));  // open: cin, cout
  Button button_1 (.out(button_1_out));
  Register #(.width(20)) DR (.D(multiplexer_1_out), .en(or_1_out), .Q(out_5), .clk(in_4), .clr(button_1_out));
endmodule

// DR Control
module DR_control (
  input  [19:0] IR,
  input  in_2,
  output Load,
  output Increment
);

  wire and_1_out, and_2_out, and_3_out, and_4_out, button_1_out, clock_1_out, decoder_1_out0, decoder_1_out1,
       decoder_1_out2, decoder_1_out3, decoder_1_out4, decoder_1_out5, decoder_1_out6, decoder_1_out7,
       decoder_2_out0, decoder_2_out1, decoder_2_out2, decoder_2_out3, decoder_2_out4, decoder_2_out5,
       decoder_2_out6, decoder_2_out7, decoder_2_out8, decoder_2_out9, decoder_2_out10, decoder_2_out11,
       decoder_2_out12, decoder_2_out13, decoder_2_out14, decoder_2_out15;
  wire [2:0] counter_1_q;

  Counter #(.width(3), .max('h7)) counter_1 (
    .load(in_2), .Q(counter_1_q), .clk(clock_1_out), .clr(button_1_out));  // open: D, count, carry
  Clock clock_1 (.out(clock_1_out));
  Button button_1 (.out(button_1_out));
  Decoder #(.select(3)) decoder_1 (
    .out0(decoder_1_out0), .out1(decoder_1_out1), .out2(decoder_1_out2), .out3(decoder_1_out3),
    .out4(decoder_1_out4), .out5(decoder_1_out5), .out6(decoder_1_out6), .out7(decoder_1_out7),
    .sel(counter_1_q));  // open: en
  Decoder #(.select(4)) decoder_2 (
    .out0(decoder_2_out0), .out1(decoder_2_out1), .out2(decoder_2_out2), .out3(decoder_2_out3),
    .out4(decoder_2_out4), .out5(decoder_2_out5), .out6(decoder_2_out6), .out7(decoder_2_out7),
    .out8(decoder_2_out8), .out9(decoder_2_out9), .out10(decoder_2_out10), .out11(decoder_2_out11),
    .out12(decoder_2_out12), .out13(decoder_2_out13), .out14(decoder_2_out14), .out15(decoder_2_out15),
    .sel(IR[17:14]));  // open: en
  and and_1 (and_1_out, ~decoder_2_out0, ~decoder_2_out15, decoder_1_out3, ~IR[19], ~IR[18]);  // AND_Gate
  and and_2 (and_2_out, ~decoder_2_out0, ~decoder_2_out15, decoder_1_out4, ~IR[19], IR[18]);  // AND_Gate
  and and_3 (and_3_out, ~decoder_2_out0, ~decoder_2_out15, decoder_1_out3, IR[19], ~IR[18]);  // AND_Gate
  and and_4 (and_4_out, decoder_2_out9, decoder_1_out6);
  and and_5 (Increment, decoder_2_out8, decoder_1_out5);
  or or_1 (Load, and_1_out, and_2_out, and_3_out, and_4_out);
endmodule

module IR (
  input  in_1,
  input  in_2,
  input  [19:0] CBS_Mockup,
  input  in_4,
  output [19:0] out_5
);

  wire button_1_out, ir_control_1_load;

  IR_control ir_control_1 (.in_1(in_1), .R(in_2), .Load(ir_control_1_load));
  Button button_1 (.out(button_1_out));
  Register #(.width(20)) IR (.D(CBS_Mockup), .en(ir_control_1_load), .Q(out_5), .clk(in_4), .clr(button_1_out));
endmodule

module IR_control (
  input  in_1,
  input  R,
  output Load
);

  wire button_1_out, clock_1_out, decoder_1_out0, decoder_1_out1, decoder_1_out2, decoder_1_out3,
       decoder_1_out4, decoder_1_out5, decoder_1_out6, decoder_1_out7;
  wire [2:0] counter_1_q;

  Counter #(.width(3), .max('h7)) counter_1 (
    .load(in_1), .Q(counter_1_q), .clk(clock_1_out), .clr(button_1_out));  // open: D, count, carry
  Clock clock_1 (.out(clock_1_out));
  Button button_1 (.out(button_1_out));
  Decoder #(.select(3)) decoder_1 (
    .out0(decoder_1_out0), .out1(decoder_1_out1), .out2(decoder_1_out2), .out3(decoder_1_out3),
    .out4(decoder_1_out4), .out5(decoder_1_out5), .out6(decoder_1_out6), .out7(decoder_1_out7),
    .sel(counter_1_q));  // open: en
  and and_1 (Load, ~R, decoder_1_out1);  // AND_Gate
endmodule

// Tiiming decoder
module Timing_decoder (
  input  Counter_Input,
  output out_2,
  output out_3,
  output out_4,
  output out_5,
  output out_6,
  output out_7,
  output out_8,
  output out_9
);

  wire button_1_out, clock_1_out;
  wire [2:0] counter_1_q;

  Clock clock_1 (.out(clock_1_out));
  Counter #(.width(3), .max('h7)) counter_1 (
    .load(Counter_Input), .Q(counter_1_q), .clk(clock_1_out), .clr(button_1_out));  // open: D, count, carry
  Button button_1 (.out(button_1_out));
  Decoder #(.select(3)) decoder_1 (
    .out0(out_2), .out1(out_3), .out2(out_4), .out3(out_5), .out4(out_6), .out5(out_7), .out6(out_8),
    .out7(out_9), .sel(counter_1_q));  // open: en
endmodule

module TR (
  input  [19:0] IR,
  input  [2:0] SC,
  input  [19:0] CBS,
  input  in_4,
  input  in_5,
  output [19:0] out_6
);

  wire button_1_out, tr_control_1_load;

  TR_control tr_control_1 (.SC(SC), .R(in_4), .IR(IR), .Load(tr_control_1_load));
  Button button_1 (.out(button_1_out));
  Register #(.width(20)) TR (.D(CBS), .en(tr_control_1_load), .Q(out_6), .clk(in_5), .clr(button_1_out));
endmodule

module TR_control (
  input  [2:0] SC,
  input  [19:0] IR,
  input  R,
  output Load
);

  wire and_1_out, and_2_out, decoder_1_out1, decoder_1_out5, decoder_2_out9;

  Decoder #(.select(3), .enable("false")) decoder_1 (
    .out1(decoder_1_out1), .out5(decoder_1_out5), .sel(SC));  // open: out0, out2, out3, out4, out6, out7
  Decoder #(.select(4), .enable("false")) decoder_2 (
    .out9(decoder_2_out9), .sel(IR[17:14]));  // open: out0, out1, out2, out3, out4, out5, out6, out7, out8, out10, out11, out12, out13, out14, out15
  and and_1 (and_1_out, decoder_1_out1, R);
  and and_2 (and_2_out, decoder_1_out5, decoder_2_out9);
  or or_1 (Load, and_1_out, and_2_out);

  // Notes on the sheet:
  //   3x8 decoder
  //   4x16 decoder
endmodule

module I0_flip_flop (
  input  R,
  input  [19:0] IR,
  input  [2:0] SC,
  input  clk,
  output I0_Value
);

  wire i0_flip_flop_control_1_j, i0_flip_flop_control_1_k;

  I0_Flip_flop_control i0_flip_flop_control_1 (
    .SC(SC), .J(i0_flip_flop_control_1_j), .K(i0_flip_flop_control_1_k), .IR(IR), .R(R));
  J_K_Flip_Flop I0 (
    .J(i0_flip_flop_control_1_j), .clk(clk), .K(i0_flip_flop_control_1_k), .Q(I0_Value));  // open: Qn, preset, en, reset
endmodule

// I0 Flip-flop Control
module I0_Flip_flop_control (
  input  [2:0] SC,
  input  R,
  input  [19:0] IR,
  output J,
  output K
);

  wire and_1_out, decoder_1_out2, not_1_out, not_2_out;

  Decoder #(.select(3), .enable("false")) decoder_1 (
    .out2(decoder_1_out2), .sel(SC));  // open: out0, out1, out3, out4, out5, out6, out7
  not not_1 (not_1_out, R);
  and and_1 (and_1_out, decoder_1_out2, not_1_out);
  not not_2 (not_2_out, IR[18]);
  and and_2 (J, and_1_out, IR[18]);
  and and_3 (K, and_1_out, not_2_out);

  // Notes on the sheet:
  //   3x8 decoder
endmodule

module I1_Flip_flop (
  input  R,
  input  [19:0] IR,
  input  [2:0] SC,
  input  clk,
  output I1_value
);

  wire i1_flip_flop_control_1_j, i1_flip_flop_control_1_k;

  I1_Flip_flop_control i1_flip_flop_control_1 (
    .SC(SC), .R(R), .J(i1_flip_flop_control_1_j), .K(i1_flip_flop_control_1_k), .IR(IR));
  J_K_Flip_Flop I1 (
    .J(i1_flip_flop_control_1_j), .clk(clk), .K(i1_flip_flop_control_1_k), .Q(I1_value));  // open: Qn, preset, en, reset
endmodule

module I1_Flip_flop_control (
  input  [2:0] SC,
  input  R,
  input  [19:0] IR,
  output J,
  output K
);

  wire and_1_out, decoder_1_out2, not_1_out, not_2_out;

  Decoder #(.select(3), .enable("false")) decoder_1 (
    .out2(decoder_1_out2), .sel(SC));  // open: out0, out1, out3, out4, out5, out6, out7
  not not_1 (not_1_out, R);
  and and_1 (and_1_out, decoder_1_out2, not_1_out);
  not not_2 (not_2_out, IR[19]);
  and and_2 (J, and_1_out, IR[19]);
  and and_3 (K, and_1_out, not_2_out);

  // Notes on the sheet:
  //   3x8 decoder
endmodule

module R_Flip_flop_control (
  input  [2:0] SC,
  input  R,
  input  IEN,
  input  FGI,
  input  FGO,
  output K,
  output J
);

  wire decoder_1_out0, decoder_1_out1, decoder_1_out2, decoder_1_out3, not_1_out, not_2_out, not_3_out,
       or_1_out;

  Decoder #(.select(3), .enable("false")) decoder_1 (
    .out0(decoder_1_out0), .out1(decoder_1_out1), .out2(decoder_1_out2), .out3(decoder_1_out3), .sel(SC));  // open: out4, out5, out6, out7
  not not_1 (not_1_out, decoder_1_out2);
  not not_2 (not_2_out, decoder_1_out1);
  not not_3 (not_3_out, decoder_1_out0);
  or or_1 (or_1_out, FGI, FGO);
  and and_1 (K, R, decoder_1_out3);
  and and_2 (J, not_1_out, not_2_out, not_3_out, IEN, or_1_out);

  // Notes on the sheet:
  //   3x8 decoder
endmodule

module R_Flip_flop (
  input  FGO,
  input  FGI,
  input  IEN,
  input  [2:0] SC,
  input  in_5,
  output R_value
);

  wire r_flip_flop_control_1_j, r_flip_flop_control_1_k;

  R_Flip_flop_control r_flip_flop_control_1 (
    .SC(SC), .R(R_value), .IEN(IEN), .FGI(FGI), .FGO(FGO), .K(r_flip_flop_control_1_k),
    .J(r_flip_flop_control_1_j));
  J_K_Flip_Flop R (
    .J(r_flip_flop_control_1_j), .clk(in_5), .K(r_flip_flop_control_1_k), .Q(R_value));  // open: Qn, preset, en, reset
endmodule

module IEN_Flip_flop (
  input  [19:0] IR,
  input  R,
  input  I1,
  input  [2:0] SC,
  input  I0,
  input  clk,
  output IEN_value
);

  wire ien_flip_flop_control_1_j, ien_flip_flop_control_1_k;

  IEN_Flip_flop_control ien_flip_flop_control_1 (
    .SC(SC), .R(R), .IR(IR), .J(ien_flip_flop_control_1_j), .K(ien_flip_flop_control_1_k), .I1(I1), .I0(I0));
  J_K_Flip_Flop IEN (
    .J(ien_flip_flop_control_1_j), .clk(clk), .K(ien_flip_flop_control_1_k), .Q(IEN_value));  // open: Qn, preset, en, reset
endmodule

module IEN_Flip_flop_control (
  input  [2:0] SC,
  input  [19:0] IR,
  input  I0,
  input  I1,
  input  R,
  output J,
  output K
);

  wire and_3_out, and_4_out, decoder_1_out3, decoder_2_out15, p;

  Decoder #(.select(3), .enable("false")) decoder_1 (
    .out3(decoder_1_out3), .sel(SC));  // open: out0, out1, out2, out4, out5, out6, out7
  Decoder #(.select(4), .enable("false")) decoder_2 (
    .out15(decoder_2_out15), .sel(IR[17:14]));  // open: out0, out1, out2, out3, out4, out5, out6, out7, out8, out9, out10, out11, out12, out13, out14
  and and_1 (p, decoder_2_out15, decoder_1_out3, I0, I1);
  and and_2 (J, IR[9], p);
  and and_3 (and_3_out, p, IR[8]);
  and and_4 (and_4_out, R, decoder_1_out3);
  or or_1 (K, and_3_out, and_4_out);

  // Notes on the sheet:
  //   3x8 decoder
  //   4x16 decoder
endmodule

module FGI_Flip_flop (
  input  I2,
  input  [19:0] IR,
  input  I1,
  input  [2:0] SC,
  input  clk,
  output FGI_value
);

  wire fgi_flip_flop_control_1_k;

  FGI_Flip_flop_control fgi_flip_flop_control_1 (.SC(SC), .IR(IR), .K(fgi_flip_flop_control_1_k), .I0(I2), .I1(I1));
  J_K_Flip_Flop FGI (.J(1'b0), .clk(clk), .K(fgi_flip_flop_control_1_k), .Q(FGI_value));  // open: Qn, preset, en, reset
endmodule

module FGI_Flip_flop_control (
  input  [2:0] SC,
  input  [19:0] IR,
  input  I0,
  input  I1,
  output K
);

  wire and_1_out, decoder_1_out3, decoder_2_out15;

  Decoder #(.select(3), .enable("false")) decoder_1 (
    .out3(decoder_1_out3), .sel(SC));  // open: out0, out1, out2, out4, out5, out6, out7
  Decoder #(.select(4), .enable("false")) decoder_2 (
    .out15(decoder_2_out15), .sel(IR[17:14]));  // open: out0, out1, out2, out3, out4, out5, out6, out7, out8, out9, out10, out11, out12, out13, out14
  and and_1 (and_1_out, decoder_2_out15, decoder_1_out3, I0, I1);
  and and_2 (K, IR[13], and_1_out);

  // Notes on the sheet:
  //   3x8 decoder
  //   4x16 decoder
endmodule

module FGO_Flip_flop (
  input  I1,
  input  I0,
  input  [19:0] IR,
  input  [2:0] SC,
  input  clk,
  output FGO_value
);

  wire fgo_flip_flop_control_1_k;

  FGO_Flip_flop_control fgo_flip_flop_control_1 (.SC(SC), .IR(IR), .K(fgo_flip_flop_control_1_k), .I0(I0), .I1(I1));
  J_K_Flip_Flop FGO (.J(1'b0), .clk(clk), .K(fgo_flip_flop_control_1_k), .Q(FGO_value));  // open: Qn, preset, en, reset
endmodule

module FGO_Flip_flop_control (
  input  [2:0] SC,
  input  [19:0] IR,
  input  I0,
  input  I1,
  output K
);

  wire and_1_out, decoder_1_out3, decoder_2_out15;

  Decoder #(.select(3), .enable("false")) decoder_1 (
    .out3(decoder_1_out3), .sel(SC));  // open: out0, out1, out2, out4, out5, out6, out7
  Decoder #(.select(4), .enable("false")) decoder_2 (
    .out15(decoder_2_out15), .sel(IR[17:14]));  // open: out0, out1, out2, out3, out4, out5, out6, out7, out8, out9, out10, out11, out12, out13, out14
  and and_1 (and_1_out, decoder_2_out15, decoder_1_out3, I0, I1);
  and and_2 (K, IR[12], and_1_out);

  // Notes on the sheet:
  //   3x8 decoder
  //   4x16 decoder
endmodule

module S_Flip_flop (
  input  I1,
  input  I0,
  input  [19:0] IR,
  input  [2:0] SC,
  input  clk,
  output S_value
);

  wire not_1_out, s_flip_flop_control_1_k;

  S_Flip_flop_control s_flip_flop_control_1 (.SC(SC), .IR(IR), .K(s_flip_flop_control_1_k), .I0(I0), .I1(I1));
  not not_1 (not_1_out, s_flip_flop_control_1_k);
  J_K_Flip_Flop S (.J(not_1_out), .clk(clk), .K(s_flip_flop_control_1_k), .Q(S_value));  // open: Qn, preset, en, reset
endmodule

module S_Flip_flop_control (
  input  [2:0] SC,
  input  [19:0] IR,
  input  I0,
  input  I1,
  output K
);

  wire and_1_out, decoder_1_out3, decoder_2_out0;

  Decoder #(.select(3), .enable("false")) decoder_1 (
    .out3(decoder_1_out3), .sel(SC));  // open: out0, out1, out2, out4, out5, out6, out7
  Decoder #(.select(4), .enable("false")) decoder_2 (
    .out0(decoder_2_out0), .sel(IR[17:14]));  // open: out1, out2, out3, out4, out5, out6, out7, out8, out9, out10, out11, out12, out13, out14, out15
  and and_1 (and_1_out, decoder_2_out0, decoder_1_out3, I0, I1);
  and and_2 (K, IR[2], and_1_out);

  // Notes on the sheet:
  //   3x8 decoder
  //   4x16 decoder
endmodule

module E_Flip_flop (
  input  Cout,
  input  [19:0] IR,
  input  I1,
  input  I0,
  input  [19:0] AC,
  input  [2:0] SC,
  input  clk,
  output E
);

  wire e_flip_flop_control_1_j, e_flip_flop_control_1_k;

  E_Flip_flop_control e_flip_flop_control_1 (
    .SC(SC), .AC(AC), .IR(IR), .Cout(Cout), .I0(I0), .I1(I1), .J(e_flip_flop_control_1_j),
    .K(e_flip_flop_control_1_k));
  J_K_Flip_Flop j_k_ff_1 (
    .J(e_flip_flop_control_1_j), .clk(clk), .K(e_flip_flop_control_1_k), .Q(E));  // open: Qn, preset, en, reset
endmodule

module E_Flip_flop_control (
  input  [2:0] SC,
  input  [19:0] IR,
  input  [19:0] AC,
  input  I1,
  input  I0,
  input  Cout,
  output J,
  output K
);

  wire and_2_out, and_3_out, and_4_out, and_5_out, and_6_out, and_7_out, and_8_out, and_9_out, and_10_out,
       and_11_out, and_12_out, decoder_1_out3, decoder_1_out5, decoder_2_out0, decoder_2_out2, not_1_out,
       not_2_out, not_3_out, r;

  Decoder #(.select(3), .enable("false")) decoder_1 (
    .out3(decoder_1_out3), .out5(decoder_1_out5), .sel(SC));  // open: out0, out1, out2, out4, out6, out7
  Decoder #(.select(4), .enable("false")) decoder_2 (
    .out0(decoder_2_out0), .out2(decoder_2_out2), .sel(IR[17:14]));  // open: out1, out3, out4, out5, out6, out7, out8, out9, out10, out11, out12, out13, out14, out15
  and and_1 (r, decoder_2_out0, decoder_1_out3, I0, I1);
  and and_2 (and_2_out, decoder_2_out2, decoder_1_out5);
  and and_3 (and_3_out, r, IR[8]);
  and and_4 (and_4_out, r, IR[9]);
  and and_5 (and_5_out, r, IR[10]);
  and and_6 (and_6_out, r, IR[12]);
  and and_7 (and_7_out, and_4_out, AC[0]);
  or or_1 (J, and_5_out, and_7_out, and_8_out, and_10_out);
  and and_8 (and_8_out, and_3_out, AC[19]);
  not not_1 (not_1_out, AC[19]);
  not not_2 (not_2_out, Cout);
  and and_9 (and_9_out, not_2_out, and_2_out);
  and and_10 (and_10_out, and_2_out, Cout);
  or or_2 (K, and_9_out, and_6_out, and_5_out, and_11_out, and_12_out);
  not not_3 (not_3_out, AC[0]);
  and and_11 (and_11_out, and_4_out, not_3_out);
  and and_12 (and_12_out, and_3_out, not_1_out);

  // Notes on the sheet:
  //   3x8 decoder
  //   4x16 decoder
  //   rB8
  //   rB9
  //   rB10
  //   rB12
  //   D2T5
endmodule
